// Logisim project JKMestreEscravo.circ as structural Verilog
module numeros (
  input  in_1,
  output [3:0] out_2
);

  wire button_1_out, button_2_out, button_3_out, button_4_out, button_5_out, button_6_out, button_7_out,
       button_8_out, clock_1_out, not_1_out, not_2_out, not_3_out, not_4_out, not_5_out, not_6_out,
       not_7_out, not_8_out;

  Clock clock_1 (.out(clock_1_out));
  not not_1 (not_1_out, button_1_out);
  Button button_1 (.out(button_1_out));
  not not_2 (not_2_out, button_2_out);
  Button button_2 (.out(button_2_out));
  JKME jkme_1 (.Set(not_1_out), .J(in_1), .Cock(clock_1_out), .K(in_1), .Reset(not_2_out), .Q(out_2[0]));  // open: NQ
  not not_3 (not_3_out, button_3_out);
  Button button_3 (.out(button_3_out));
  not not_4 (not_4_out, button_4_out);
  Button button_4 (.out(button_4_out));
  Hex_Digit_Display hex_digit_display_1 (.value(out_2));  // open: dp
  JKME jkme_2 (.Set(not_3_out), .J(in_1), .Cock(out_2[0]), .K(in_1), .Reset(not_4_out), .Q(out_2[1]));  // open: NQ
  not not_5 (not_5_out, button_5_out);
  Button button_5 (.out(button_5_out));
  not not_6 (not_6_out, button_6_out);
  Button button_6 (.out(button_6_out));
  JKME jkme_3 (.Set(not_5_out), .J(in_1), .Cock(out_2[1]), .K(in_1), .Reset(not_6_out), .Q(out_2[2]));  // open: NQ
  not not_7 (not_7_out, button_7_out);
  Button button_7 (.out(button_7_out));
  not not_8 (not_8_out, button_8_out);
  Button button_8 (.out(button_8_out));
  JKME jkme_4 (.Set(not_7_out), .J(in_1), .Cock(out_2[2]), .K(in_1), .Reset(not_8_out), .Q(out_2[3]));  // open: NQ
endmodule

module JKME (
  input  Set,
  input  J,
  input  Cock,
  input  K,
  input  Reset,
  output Q,
  output NQ
);

  wire nand_1_out, nand_2_out, nand_3_out, nand_4_out, nand_5_out, nand_6_out, not_1_out;

  nand nand_1 (nand_1_out, J, Cock, NQ);
  nand nand_2 (nand_2_out, Q, Cock, K);
  nand nand_3 (nand_3_out, Set, nand_1_out, nand_4_out);
  nand nand_4 (nand_4_out, nand_3_out, nand_2_out, Reset);
  not not_1 (not_1_out, Cock);
  nand nand_5 (nand_5_out, nand_3_out, not_1_out);
  nand nand_6 (nand_6_out, nand_4_out, not_1_out);
  nand nand_7 (Q, Set, nand_5_out, NQ);
  nand nand_8 (NQ, Q, nand_6_out, Reset);
endmodule
