// Logisim project flipflop_jk.circ as structural Verilog: 8 circuits, main circuit main
module main (
);

  teste teste_1 ();  // open: in_5, in_6, in_1, in_3, in_4, in_2, out_7
endmodule

module flipflopD (
  input  pset,
  input  J,
  input  clock,
  input  clear,
  output Q,
  output nQ
);

  wire nand_1_out, nand_2_out, nand_3_out, nand_4_out, nand_5_out, nand_6_out, not_1_out, not_2_out,
       not_3_out;

  not not_1 (not_1_out, J);
  not not_2 (not_2_out, pset);
  nand nand_1 (nand_1_out, J, clock, nQ);
  nand nand_2 (nand_2_out, Q, clock, not_1_out);
  not not_3 (not_3_out, clear);
  nand nand_3 (nand_3_out, not_2_out, nand_1_out, nand_4_out);
  nand nand_4 (nand_4_out, nand_3_out, nand_2_out, not_3_out);
  nand nand_5 (nand_5_out, ~clock, nand_3_out);  // NAND_Gate
  nand nand_6 (nand_6_out, nand_4_out, ~clock);  // NAND_Gate
  nand nand_7 (Q, not_2_out, nand_5_out, nQ);
  nand nand_8 (nQ, Q, nand_6_out, not_3_out);
endmodule

module jk (
  input  in_1,
  input  in_2,
  output out_3,
  output out_4
);

  wire clock_1_out, nand_1_out, nand_2_out;

  Clock clock_1 (.out(clock_1_out));
  nand nand_1 (nand_1_out, in_1, clock_1_out, out_4);
  nand nand_2 (nand_2_out, out_3, clock_1_out, in_2);
  nand nand_3 (out_3, nand_1_out, out_4);
  nand nand_4 (out_4, out_3, nand_2_out);
endmodule

module flipflotT (
  input  pset,
  input  J,
  input  clock,
  input  clear,
  output Q,
  output nQ
);

  wire nand_1_out, nand_2_out, nand_3_out, nand_4_out, nand_5_out, nand_6_out, not_1_out, not_2_out;

  not not_1 (not_1_out, pset);
  nand nand_1 (nand_1_out, J, clock, nQ);
  nand nand_2 (nand_2_out, Q, clock, J);
  not not_2 (not_2_out, clear);
  nand nand_3 (nand_3_out, not_1_out, nand_1_out, nand_4_out);
  nand nand_4 (nand_4_out, nand_3_out, nand_2_out, not_2_out);
  nand nand_5 (nand_5_out, ~clock, nand_3_out);  // NAND_Gate
  nand nand_6 (nand_6_out, nand_4_out, ~clock);  // NAND_Gate
  nand nand_7 (Q, not_1_out, nand_5_out, nQ);
  nand nand_8 (nQ, Q, nand_6_out, not_2_out);
endmodule

module teste (
  input  in_1,
  input  in_2,
  input  in_3,
  input  in_4,
  input  in_5,
  input  in_6,
  output [3:0] out_7
);

  wire and_1_out, and_2_out, and_3_out, and_4_out, and_5_out, and_6_out, and_7_out, and_8_out, clear_out,
       or_1_out, or_2_out, or_3_out, or_4_out, pset_out;

  Button pset (.out(pset_out));
  Button clear (.out(clear_out));
  and and_1 (and_1_out, ~in_1, pset_out);  // AND_Gate
  and and_2 (and_2_out, pset_out, in_1);
  flipflopD FFD1 (.pset(and_2_out), .J(in_5), .clock(in_6), .clear(or_1_out), .Q(out_7[0]));  // open: nQ
  or or_1 (or_1_out, and_1_out, clear_out);
  and and_3 (and_3_out, ~in_3, pset_out);  // AND_Gate
  and and_4 (and_4_out, pset_out, in_3);
  flipflopD FFD2 (.pset(and_4_out), .J(out_7[0]), .clock(in_6), .clear(or_2_out), .Q(out_7[1]));  // open: nQ
  or or_2 (or_2_out, and_3_out, clear_out);
  and and_5 (and_5_out, ~in_4, pset_out);  // AND_Gate
  or or_3 (or_3_out, and_5_out, clear_out);
  and and_6 (and_6_out, pset_out, in_4);
  flipflopD FFD3 (.pset(and_6_out), .J(out_7[1]), .clock(in_6), .clear(or_3_out), .Q(out_7[2]));  // open: nQ
  and and_7 (and_7_out, ~in_2, pset_out);  // AND_Gate
  and and_8 (and_8_out, pset_out, in_2);
  flipflopD FFD4 (.pset(and_8_out), .J(out_7[2]), .clock(in_6), .clear(or_4_out), .Q(out_7[3]));  // open: nQ
  or or_4 (or_4_out, and_7_out, clear_out);
  Hex_Digit_Display hex_digit_display_1 (.value(out_7));  // open: dp
endmodule

module mux (
  input  enable,
  input  qA,
  input  qB,
  output out_4
);

  wire and_1_out, and_2_out;

  and and_1 (and_1_out, qA, enable);
  and and_2 (and_2_out, ~enable, qB);  // AND_Gate
  or or_1 (out_4, and_1_out, and_2_out);
endmodule

module mux4bits (
  input  s0,
  input  s1,
  input  s2,
  input  s3,
  input  enable,
  output [3:0] out_6
);

  // mux mux_1: pin names not known; wires that end beside it: s0, s3, enable, out_6[0]
  // mux mux_2: pin names not known; wires that end beside it: s1, s2, enable, out_6[1]
  // mux mux_3: pin names not known; wires that end beside it: s2, s1, enable, out_6[2]
  // mux mux_4: pin names not known; wires that end beside it: s3, s0, enable, out_6[3]
endmodule

module mux_serial (
  input  enable,
  input  qA,
  input  qB,
  output out_4
);

  wire and_1_out, and_2_out;

  and and_1 (and_1_out, qA, enable);
  and and_2 (and_2_out, ~enable, qB);  // AND_Gate
  or or_1 (out_4, and_1_out, and_2_out);
endmodule
