// Logisim project flopFlip.circ as structural Verilog
module main (
  input  I3,
  input  I2,
  input  I1,
  input  I0,
  input  C1,
  input  C0,
  input  J,
  input  CK,
  input  in_9,
  input  in_10,
  input  in_11,
  input  in_12,
  input  in_13,
  output out_14
);

  wire bindisplay_1_sa, bindisplay_1_sb, bindisplay_1_sc, bindisplay_1_sd, bindisplay_1_se, bindisplay_1_sf,
       bindisplay_1_sg, bindisplay_2_sa, bindisplay_2_sb, bindisplay_2_sc, bindisplay_2_sd, bindisplay_2_se,
       bindisplay_2_sf, bindisplay_2_sg, bindisplay_3_sa, bindisplay_3_sb, bindisplay_3_sc, bindisplay_3_sd,
       bindisplay_3_se, bindisplay_3_sf, bindisplay_3_sg, bindisplay_4_sa, bindisplay_4_sb, bindisplay_4_sc,
       bindisplay_4_sd, bindisplay_4_se, bindisplay_4_sf, bindisplay_4_sg, conversor_1_a, conversor_1_b,
       conversor_1_c, conversor_1_d, conversor_1_e, conversor_1_f, conversor_1_g, mux2_1_out_7, mux2_2_out_7,
       mux2_3_out_7, mux2_4_out_7, Q0, Q1, Q2, Q3;

  BinDisplay bindisplay_1 (
    .A(Q3), .sa(bindisplay_1_sa), .sb(bindisplay_1_sb), .sc(bindisplay_1_sc), .sd(bindisplay_1_sd),
    .se(bindisplay_1_se), .sf(bindisplay_1_sf), .sg(bindisplay_1_sg));
  _7_Segment_Display u_7_segment_display_1 (
    .g(bindisplay_1_sf), .f(bindisplay_1_sg), .a(bindisplay_1_sa), .b(bindisplay_1_sb), .e(bindisplay_1_se),
    .d(bindisplay_1_sd), .c(bindisplay_1_sc));  // open: dp
  mux2 mux2_1 (.in_2(Q3), .in_4(Q2), .in_5(J), .in_6(I3), .C0(C0), .C1(C1), .out_7(mux2_1_out_7));
  BinDisplay bindisplay_2 (
    .A(Q2), .sa(bindisplay_2_sa), .sb(bindisplay_2_sb), .sc(bindisplay_2_sc), .sd(bindisplay_2_sd),
    .se(bindisplay_2_se), .sf(bindisplay_2_sf), .sg(bindisplay_2_sg));
  FFMEPSD ffmepsd_1 (.J(mux2_1_out_7), .SET(1'b1), .CLK(CK), .CLEAR(in_9), .Q(Q3));  // open: NQ
  _7_Segment_Display u_7_segment_display_2 (
    .g(bindisplay_2_sf), .f(bindisplay_2_sg), .a(bindisplay_2_sa), .b(bindisplay_2_sb), .e(bindisplay_2_se),
    .d(bindisplay_2_sd), .c(bindisplay_2_sc));  // open: dp
  BinDisplay bindisplay_3 (
    .A(Q1), .sa(bindisplay_3_sa), .sb(bindisplay_3_sb), .sc(bindisplay_3_sc), .sd(bindisplay_3_sd),
    .se(bindisplay_3_se), .sf(bindisplay_3_sf), .sg(bindisplay_3_sg));
  mux2 mux2_2 (.in_2(Q2), .in_4(Q1), .in_5(Q3), .in_6(I2), .C0(C0), .C1(C1), .out_7(mux2_2_out_7));
  _7_Segment_Display u_7_segment_display_3 (
    .g(bindisplay_3_sf), .f(bindisplay_3_sg), .a(bindisplay_3_sa), .b(bindisplay_3_sb), .e(bindisplay_3_se),
    .d(bindisplay_3_sd), .c(bindisplay_3_sc));  // open: dp
  FFMEPSD ffmepsd_2 (.J(mux2_2_out_7), .SET(1'b1), .CLK(CK), .CLEAR(in_9), .Q(Q2));  // open: NQ
  BinDisplay bindisplay_4 (
    .A(Q0), .sa(bindisplay_4_sa), .sb(bindisplay_4_sb), .sc(bindisplay_4_sc), .sd(bindisplay_4_sd),
    .se(bindisplay_4_se), .sf(bindisplay_4_sf), .sg(bindisplay_4_sg));
  jk_mestre_escravo_T jk_mestre_escravo_t_1 (
    .J(in_10), .CLK(in_11), .PRESET(in_12), .CLEAR(in_13), .Q(out_14));  // open: QN
  _7_Segment_Display u_7_segment_display_4 (
    .g(bindisplay_4_sf), .f(bindisplay_4_sg), .a(bindisplay_4_sa), .b(bindisplay_4_sb), .e(bindisplay_4_se),
    .d(bindisplay_4_sd), .c(bindisplay_4_sc));  // open: dp
  mux2 mux2_3 (.in_2(Q1), .in_4(Q0), .in_5(Q2), .in_6(I1), .C0(C0), .C1(C1), .out_7(mux2_3_out_7));
  conversor conversor_1 (
    .AA(Q3), .BB(Q2), .CC(Q1), .DD(Q0), .a(conversor_1_a), .b(conversor_1_b), .c(conversor_1_c),
    .d(conversor_1_d), .e(conversor_1_e), .f(conversor_1_f), .g(conversor_1_g));
  FFMEPSD ffmepsd_3 (.J(mux2_3_out_7), .SET(1'b1), .CLK(CK), .CLEAR(in_9), .Q(Q1));  // open: NQ
  _7_Segment_Display u_7_segment_display_5 (
    .g(conversor_1_g), .f(conversor_1_f), .a(conversor_1_a), .b(conversor_1_b), .e(conversor_1_e),
    .d(conversor_1_d), .c(conversor_1_c));  // open: dp
  mux2 mux2_4 (.in_2(Q0), .in_4(J), .in_5(Q1), .in_6(I0), .C0(C0), .C1(C1), .out_7(mux2_4_out_7));
  FFMEPSD ffmepsd_4 (.J(mux2_4_out_7), .SET(1'b1), .CLK(CK), .CLEAR(in_9), .Q(Q0));  // open: NQ

  // Other names for the same wires on the sheet: S0 = I0; S1 = I1; S2 = I2; S3 = I3
endmodule

module FFJKMEPCT (
  input  SET,
  input  J,
  input  COCK,
  input  RESET,
  output Q,
  output NQ
);

  wire nand_1_out, nand_2_out, nand_3_out, nand_4_out, nand_5_out, nand_6_out, not_1_out, not_2_out;

  not not_1 (not_1_out, J);
  nand nand_1 (nand_1_out, COCK, J, NQ);
  nand nand_2 (nand_2_out, Q, not_1_out, COCK);
  not not_2 (not_2_out, COCK);
  nand nand_3 (nand_3_out, SET, nand_1_out, nand_4_out);
  nand nand_4 (nand_4_out, nand_3_out, nand_2_out, RESET);
  nand nand_5 (nand_5_out, nand_3_out, not_2_out);
  nand nand_6 (nand_6_out, not_2_out, nand_4_out);
  nand nand_7 (Q, SET, nand_5_out, NQ);
  nand nand_8 (NQ, Q, nand_6_out, RESET);
endmodule

module Divisor_freq (
  input  in_1,
  input  in_2,
  input  in_3,
  input  in_4,
  input  J,
  input  CLK
);

  wire bihex_vhdl_1_aa, bihex_vhdl_1_bb, bihex_vhdl_1_cc, bihex_vhdl_1_dd, bihex_vhdl_1_e, bihex_vhdl_1_f,
       bihex_vhdl_1_g, bindisplay_1_sa, bindisplay_1_sb, bindisplay_1_sc, bindisplay_1_sd, bindisplay_1_se,
       bindisplay_1_sf, bindisplay_2_sa, bindisplay_2_sb, bindisplay_2_sc, bindisplay_2_sd, bindisplay_2_se,
       bindisplay_2_sf, bindisplay_2_sg, bindisplay_3_sa, bindisplay_3_sb, bindisplay_3_sc, bindisplay_3_sd,
       bindisplay_3_se, bindisplay_3_sf, bindisplay_3_sg, bindisplay_4_sa, bindisplay_4_sb, bindisplay_4_sc,
       bindisplay_4_sd, bindisplay_4_se, bindisplay_4_sf, bindisplay_4_sg, bindisplay_vhdl_1_aa,
       bindisplay_vhdl_1_b, bindisplay_vhdl_1_c, bindisplay_vhdl_1_d, bindisplay_vhdl_1_e,
       bindisplay_vhdl_1_f, bindisplay_vhdl_1_g, bindisplay_vhdl_2_aa, bindisplay_vhdl_2_b,
       bindisplay_vhdl_2_c, bindisplay_vhdl_2_d, bindisplay_vhdl_2_e, bindisplay_vhdl_2_f,
       bindisplay_vhdl_2_g, bindisplay_vhdl_3_aa, bindisplay_vhdl_3_b, bindisplay_vhdl_3_c,
       bindisplay_vhdl_3_d, bindisplay_vhdl_3_e, bindisplay_vhdl_3_f, bindisplay_vhdl_3_g,
       bindisplay_vhdl_4_aa, bindisplay_vhdl_4_b, bindisplay_vhdl_4_c, bindisplay_vhdl_4_d,
       bindisplay_vhdl_4_e, bindisplay_vhdl_4_f, bindisplay_vhdl_4_g, CLEAR_out, conversor_1_a,
       conversor_1_b, conversor_1_c, conversor_1_d, conversor_1_e, conversor_1_f, conversor_1_g, fft_1_q,
       fft_2_q, fft_3_q, fft_4_q, not_1_out, not_2_out, Q0, Q1, Q2, Q3, SET_out;

  Button SET (.out(SET_out));
  not not_1 (not_1_out, SET_out);
  FFT fft_1 (.J(J), .SET(not_1_out), .clk(CLK), .CLEAR(not_2_out), .Q(fft_1_q));  // open: NQ
  not not_2 (not_2_out, CLEAR_out);
  Button CLEAR (.out(CLEAR_out));
  BinDisplay bindisplay_1 (
    .A(fft_1_q), .sa(bindisplay_1_sa), .sb(bindisplay_1_sb), .sc(bindisplay_1_sc), .sd(bindisplay_1_sd),
    .se(bindisplay_1_se), .sf(bindisplay_1_sf), .sg(bindisplay_1_sa));
  _7_Segment_Display u_7_segment_display_1 (
    .g(bindisplay_1_sf), .f(bindisplay_1_sa), .a(bindisplay_1_sa), .b(bindisplay_1_sb), .e(bindisplay_1_se),
    .d(bindisplay_1_sd), .c(bindisplay_1_sc));  // open: dp
  FFT fft_2 (.J(J), .SET(not_1_out), .clk(fft_1_q), .CLEAR(not_2_out), .Q(fft_2_q));  // open: NQ
  BinDisplay bindisplay_2 (
    .A(fft_2_q), .sa(bindisplay_2_sa), .sb(bindisplay_2_sb), .sc(bindisplay_2_sc), .sd(bindisplay_2_sd),
    .se(bindisplay_2_se), .sf(bindisplay_2_sf), .sg(bindisplay_2_sg));
  _7_Segment_Display u_7_segment_display_2 (
    .g(bindisplay_2_sf), .f(bindisplay_2_sg), .a(bindisplay_2_sa), .b(bindisplay_2_sb), .e(bindisplay_2_se),
    .d(bindisplay_2_sd), .c(bindisplay_2_sc));  // open: dp
  BinDisplay bindisplay_3 (
    .A(fft_3_q), .sa(bindisplay_3_sa), .sb(bindisplay_3_sb), .sc(bindisplay_3_sc), .sd(bindisplay_3_sd),
    .se(bindisplay_3_se), .sf(bindisplay_3_sf), .sg(bindisplay_3_sg));
  FFT fft_3 (.J(J), .SET(not_1_out), .clk(fft_2_q), .CLEAR(not_2_out), .Q(fft_3_q));  // open: NQ
  _7_Segment_Display u_7_segment_display_3 (
    .g(bindisplay_3_sf), .f(bindisplay_3_sg), .a(bindisplay_3_sa), .b(bindisplay_3_sb), .e(bindisplay_3_se),
    .d(bindisplay_3_sd), .c(bindisplay_3_sc));  // open: dp
  FFT fft_4 (.J(J), .SET(not_1_out), .clk(fft_3_q), .CLEAR(not_2_out), .Q(fft_4_q));  // open: NQ
  BinDisplay bindisplay_4 (
    .A(fft_4_q), .sa(bindisplay_4_sa), .sb(bindisplay_4_sb), .sc(bindisplay_4_sc), .sd(bindisplay_4_sd),
    .se(bindisplay_4_se), .sf(bindisplay_4_sf), .sg(bindisplay_4_sg));
  _7_Segment_Display u_7_segment_display_4 (
    .g(bindisplay_4_sf), .f(bindisplay_4_sg), .a(bindisplay_4_sa), .b(bindisplay_4_sb), .e(bindisplay_4_se),
    .d(bindisplay_4_sd), .c(bindisplay_4_sc));  // open: dp
  conversor conversor_1 (
    .AA(fft_4_q), .BB(fft_3_q), .CC(fft_2_q), .DD(fft_1_q), .a(conversor_1_a), .b(conversor_1_b),
    .c(conversor_1_c), .d(conversor_1_d), .e(conversor_1_e), .f(conversor_1_f), .g(conversor_1_g));
  _7_Segment_Display displayA (
    .g(conversor_1_g), .f(conversor_1_f), .a(conversor_1_a), .b(conversor_1_b), .e(conversor_1_e),
    .d(conversor_1_d), .c(conversor_1_c));  // open: dp
  BinDisplay_VHDL bindisplay_vhdl_1 (
    .A(Q3), .aa(bindisplay_vhdl_1_aa), .b(bindisplay_vhdl_1_b), .c(bindisplay_vhdl_1_c),
    .d(bindisplay_vhdl_1_d), .e(bindisplay_vhdl_1_e), .f(bindisplay_vhdl_1_f), .g(bindisplay_vhdl_1_g));
  _7_Segment_Display u_7_segment_display_5 (
    .g(bindisplay_vhdl_1_f), .f(bindisplay_vhdl_1_g), .a(bindisplay_vhdl_1_aa), .b(bindisplay_vhdl_1_b),
    .e(bindisplay_vhdl_1_e), .d(bindisplay_vhdl_1_d), .c(bindisplay_vhdl_1_c));  // open: dp
  BinDisplay_VHDL bindisplay_vhdl_2 (
    .A(Q2), .aa(bindisplay_vhdl_2_aa), .b(bindisplay_vhdl_2_b), .c(bindisplay_vhdl_2_c),
    .d(bindisplay_vhdl_2_d), .e(bindisplay_vhdl_2_e), .f(bindisplay_vhdl_2_f), .g(bindisplay_vhdl_2_g));
  _7_Segment_Display u_7_segment_display_6 (
    .g(bindisplay_vhdl_2_f), .f(bindisplay_vhdl_2_g), .a(bindisplay_vhdl_2_aa), .b(bindisplay_vhdl_2_b),
    .e(bindisplay_vhdl_2_e), .d(bindisplay_vhdl_2_d), .c(bindisplay_vhdl_2_c));  // open: dp
  Divisor_freq_VHDL divisor_freq_vhdl_1 (.SET(in_1), .CLOCK(in_2), .J(in_3), .CLEAR(in_4), .S({Q3, Q2, Q1, Q0}));
  BinDisplay_VHDL bindisplay_vhdl_3 (
    .A(Q1), .aa(bindisplay_vhdl_3_aa), .b(bindisplay_vhdl_3_b), .c(bindisplay_vhdl_3_c),
    .d(bindisplay_vhdl_3_d), .e(bindisplay_vhdl_3_e), .f(bindisplay_vhdl_3_f), .g(bindisplay_vhdl_3_g));
  _7_Segment_Display u_7_segment_display_7 (
    .g(bindisplay_vhdl_3_f), .f(bindisplay_vhdl_3_g), .a(bindisplay_vhdl_3_aa), .b(bindisplay_vhdl_3_b),
    .e(bindisplay_vhdl_3_e), .d(bindisplay_vhdl_3_d), .c(bindisplay_vhdl_3_c));  // open: dp
  BinDisplay_VHDL bindisplay_vhdl_4 (
    .A(Q0), .aa(bindisplay_vhdl_4_aa), .b(bindisplay_vhdl_4_b), .c(bindisplay_vhdl_4_c),
    .d(bindisplay_vhdl_4_d), .e(bindisplay_vhdl_4_e), .f(bindisplay_vhdl_4_f), .g(bindisplay_vhdl_4_g));
  _7_Segment_Display u_7_segment_display_8 (
    .g(bindisplay_vhdl_4_f), .f(bindisplay_vhdl_4_g), .a(bindisplay_vhdl_4_aa), .b(bindisplay_vhdl_4_b),
    .e(bindisplay_vhdl_4_e), .d(bindisplay_vhdl_4_d), .c(bindisplay_vhdl_4_c));  // open: dp
  BiHex_VHDL bihex_vhdl_1 (
    .A(Q3), .B(Q2), .C(Q1), .D(Q0), .aa(bihex_vhdl_1_aa), .bb(bihex_vhdl_1_bb), .cc(bihex_vhdl_1_cc),
    .dd(bihex_vhdl_1_dd), .e(bihex_vhdl_1_e), .f(bihex_vhdl_1_f), .g(bihex_vhdl_1_g));
  _7_Segment_Display u_7_segment_display_9 (
    .g(bihex_vhdl_1_g), .f(bihex_vhdl_1_f), .a(bihex_vhdl_1_aa), .b(bihex_vhdl_1_bb), .e(bihex_vhdl_1_e),
    .d(bihex_vhdl_1_dd), .c(bihex_vhdl_1_cc));  // open: dp

  // Notes on the sheet:
  //   SAÍDA-PARELELA
  //   SAÍDA-SERIAL
  //   SAÍDA-PARALELA-VHDL
  //   SÁIDA-SERIAL-VHDL
endmodule

module Registrador_divisor (
  input  S3,
  input  S0,
  input  S2,
  input  S1,
  input  J,
  input  CLK
);

  wire and_1_out, and_2_out, and_3_out, and_4_out, and_5_out, and_6_out, and_7_out, and_8_out,
       bihex_vhdl_1_aa, bihex_vhdl_1_bb, bihex_vhdl_1_cc, bihex_vhdl_1_dd, bihex_vhdl_1_e, bihex_vhdl_1_f,
       bihex_vhdl_1_g, bindisplay_1_sa, bindisplay_1_sb, bindisplay_1_sc, bindisplay_1_sd, bindisplay_1_se,
       bindisplay_1_sf, bindisplay_1_sg, bindisplay_2_sa, bindisplay_2_sb, bindisplay_2_sc, bindisplay_2_sd,
       bindisplay_2_se, bindisplay_2_sf, bindisplay_2_sg, bindisplay_3_sa, bindisplay_3_sb, bindisplay_3_sc,
       bindisplay_3_sd, bindisplay_3_se, bindisplay_3_sf, bindisplay_3_sg, bindisplay_4_sa, bindisplay_4_sb,
       bindisplay_4_sc, bindisplay_4_sd, bindisplay_4_se, bindisplay_4_sf, bindisplay_4_sg, bindisplay_5_sa,
       bindisplay_5_sb, bindisplay_5_sc, bindisplay_5_sd, bindisplay_5_se, bindisplay_5_sf, bindisplay_5_sg,
       bindisplay_6_sa, bindisplay_6_sb, bindisplay_6_sc, bindisplay_6_sd, bindisplay_6_se, bindisplay_6_sf,
       bindisplay_6_sg, bindisplay_7_sa, bindisplay_7_sb, bindisplay_7_sc, bindisplay_7_sd, bindisplay_7_se,
       bindisplay_7_sf, bindisplay_7_sg, bindisplay_8_sa, bindisplay_8_sb, bindisplay_8_sc, bindisplay_8_sd,
       bindisplay_8_se, bindisplay_8_sf, bindisplay_8_sg, bindisplay_vhdl_1_aa, bindisplay_vhdl_1_b,
       bindisplay_vhdl_1_c, bindisplay_vhdl_1_d, bindisplay_vhdl_1_e, bindisplay_vhdl_1_f,
       bindisplay_vhdl_1_g, bindisplay_vhdl_2_aa, bindisplay_vhdl_2_b, bindisplay_vhdl_2_c,
       bindisplay_vhdl_2_d, bindisplay_vhdl_2_e, bindisplay_vhdl_2_f, bindisplay_vhdl_2_g,
       bindisplay_vhdl_3_aa, bindisplay_vhdl_3_b, bindisplay_vhdl_3_c, bindisplay_vhdl_3_d,
       bindisplay_vhdl_3_e, bindisplay_vhdl_3_f, bindisplay_vhdl_3_g, bindisplay_vhdl_4_aa,
       bindisplay_vhdl_4_b, bindisplay_vhdl_4_c, bindisplay_vhdl_4_d, bindisplay_vhdl_4_e,
       bindisplay_vhdl_4_f, bindisplay_vhdl_4_g, CLEAR_out, conversor_1_a, conversor_1_b, conversor_1_c,
       conversor_1_d, conversor_1_e, conversor_1_f, conversor_1_g, not_1_out, not_2_out, not_3_out,
       not_4_out, not_5_out, not_6_out, not_7_out, not_8_out, not_9_out, not_10_out, or_1_out, or_2_out,
       or_3_out, or_4_out, Q0, Q1, Q2, Q3, SET_out, VQ0, VQ1, VQ2, VQ3;

  BinDisplay bindisplay_1 (
    .A(Q0), .sa(bindisplay_1_sa), .sb(bindisplay_1_sb), .sc(bindisplay_1_sc), .sd(bindisplay_1_sd),
    .se(bindisplay_1_se), .sf(bindisplay_1_sf), .sg(bindisplay_1_sg));
  _7_Segment_Display u_7_segment_display_1 (
    .g(bindisplay_1_sf), .f(bindisplay_1_sg), .a(bindisplay_1_sa), .b(bindisplay_1_sb), .e(bindisplay_1_se),
    .d(bindisplay_1_sd), .c(bindisplay_1_sc));  // open: dp
  Button SET (.out(SET_out));
  Button CLEAR (.out(CLEAR_out));
  BinDisplay bindisplay_2 (
    .A(Q1), .sa(bindisplay_2_sa), .sb(bindisplay_2_sb), .sc(bindisplay_2_sc), .sd(bindisplay_2_sd),
    .se(bindisplay_2_se), .sf(bindisplay_2_sf), .sg(bindisplay_2_sg));
  BinDisplay bindisplay_3 (
    .A(S3), .sa(bindisplay_3_sa), .sb(bindisplay_3_sb), .sc(bindisplay_3_sc), .sd(bindisplay_3_sd),
    .se(bindisplay_3_se), .sf(bindisplay_3_sf), .sg(bindisplay_3_sg));
  _7_Segment_Display u_7_segment_display_2 (
    .g(bindisplay_2_sf), .f(bindisplay_2_sg), .a(bindisplay_2_sa), .b(bindisplay_2_sb), .e(bindisplay_2_se),
    .d(bindisplay_2_sd), .c(bindisplay_2_sc));  // open: dp
  and and_1 (and_1_out, SET_out, S3);
  not not_1 (not_1_out, and_1_out);
  and and_2 (and_2_out, ~S3, SET_out);  // AND_Gate
  or or_1 (or_1_out, and_2_out, CLEAR_out);
  not not_2 (not_2_out, or_1_out);
  _7_Segment_Display u_7_segment_display_3 (
    .g(bindisplay_3_sf), .f(bindisplay_3_sg), .a(bindisplay_3_sa), .b(bindisplay_3_sb), .e(bindisplay_3_se),
    .d(bindisplay_3_sd), .c(bindisplay_3_sc));  // open: dp
  FFMEPSD ffmepsd_1 (.J(J), .SET(not_1_out), .CLK(CLK), .CLEAR(not_2_out), .Q(Q0));  // open: NQ
  BinDisplay bindisplay_4 (
    .A(S2), .sa(bindisplay_4_sa), .sb(bindisplay_4_sb), .sc(bindisplay_4_sc), .sd(bindisplay_4_sd),
    .se(bindisplay_4_se), .sf(bindisplay_4_sf), .sg(bindisplay_4_sg));
  BinDisplay bindisplay_5 (
    .A(Q2), .sa(bindisplay_5_sa), .sb(bindisplay_5_sb), .sc(bindisplay_5_sc), .sd(bindisplay_5_sd),
    .se(bindisplay_5_se), .sf(bindisplay_5_sf), .sg(bindisplay_5_sg));
  and and_3 (and_3_out, SET_out, S2);
  not not_3 (not_3_out, and_3_out);
  and and_4 (and_4_out, ~S2, SET_out);  // AND_Gate
  or or_2 (or_2_out, and_4_out, CLEAR_out);
  not not_4 (not_4_out, or_2_out);
  _7_Segment_Display u_7_segment_display_4 (
    .g(bindisplay_4_sf), .f(bindisplay_4_sg), .a(bindisplay_4_sa), .b(bindisplay_4_sb), .e(bindisplay_4_se),
    .d(bindisplay_4_sd), .c(bindisplay_4_sc));  // open: dp
  _7_Segment_Display u_7_segment_display_5 (
    .g(bindisplay_5_sf), .f(bindisplay_5_sg), .a(bindisplay_5_sa), .b(bindisplay_5_sb), .e(bindisplay_5_se),
    .d(bindisplay_5_sd), .c(bindisplay_5_sc));  // open: dp
  FFMEPSD ffmepsd_2 (.J(Q0), .SET(not_3_out), .CLK(CLK), .CLEAR(not_4_out), .Q(Q1));  // open: NQ
  and and_5 (and_5_out, ~S1, SET_out);  // AND_Gate
  BinDisplay bindisplay_6 (
    .A(Q3), .sa(bindisplay_6_sa), .sb(bindisplay_6_sb), .sc(bindisplay_6_sc), .sd(bindisplay_6_sd),
    .se(bindisplay_6_se), .sf(bindisplay_6_sf), .sg(bindisplay_6_sg));
  and and_6 (and_6_out, SET_out, S1);
  not not_5 (not_5_out, and_6_out);
  or or_3 (or_3_out, and_5_out, CLEAR_out);
  not not_6 (not_6_out, or_3_out);
  BinDisplay bindisplay_7 (
    .A(S1), .sa(bindisplay_7_sa), .sb(bindisplay_7_sb), .sc(bindisplay_7_sc), .sd(bindisplay_7_sd),
    .se(bindisplay_7_se), .sf(bindisplay_7_sf), .sg(bindisplay_7_sg));
  _7_Segment_Display u_7_segment_display_6 (
    .g(bindisplay_6_sf), .f(bindisplay_6_sg), .a(bindisplay_6_sa), .b(bindisplay_6_sb), .e(bindisplay_6_se),
    .d(bindisplay_6_sd), .c(bindisplay_6_sc));  // open: dp
  FFMEPSD ffmepsd_3 (.J(Q1), .SET(not_5_out), .CLK(CLK), .CLEAR(not_6_out), .Q(Q2));  // open: NQ
  and and_7 (and_7_out, ~S0, SET_out);  // AND_Gate
  _7_Segment_Display u_7_segment_display_7 (
    .g(bindisplay_7_sf), .f(bindisplay_7_sg), .a(bindisplay_7_sa), .b(bindisplay_7_sb), .e(bindisplay_7_se),
    .d(bindisplay_7_sd), .c(bindisplay_7_sc));  // open: dp
  and and_8 (and_8_out, SET_out, S0);
  not not_7 (not_7_out, and_8_out);
  FFMEPSD ffmepsd_4 (.J(Q2), .SET(not_7_out), .CLK(CLK), .CLEAR(not_8_out), .Q(Q3));  // open: NQ
  or or_4 (or_4_out, and_7_out, CLEAR_out);
  not not_8 (not_8_out, or_4_out);
  conversor conversor_1 (
    .AA(Q0), .BB(Q1), .CC(Q2), .DD(Q3), .a(conversor_1_a), .b(conversor_1_b), .c(conversor_1_c),
    .d(conversor_1_d), .e(conversor_1_e), .f(conversor_1_f), .g(conversor_1_g));
  BinDisplay bindisplay_8 (
    .A(S0), .sa(bindisplay_8_sa), .sb(bindisplay_8_sb), .sc(bindisplay_8_sc), .sd(bindisplay_8_sd),
    .se(bindisplay_8_se), .sf(bindisplay_8_sf), .sg(bindisplay_8_sg));
  _7_Segment_Display u_7_segment_display_8 (
    .g(conversor_1_g), .f(conversor_1_f), .a(conversor_1_a), .b(conversor_1_b), .e(conversor_1_e),
    .d(conversor_1_d), .c(conversor_1_c));  // open: dp
  _7_Segment_Display u_7_segment_display_9 (
    .g(bindisplay_8_sf), .f(bindisplay_8_sg), .a(bindisplay_8_sa), .b(bindisplay_8_sb), .e(bindisplay_8_se),
    .d(bindisplay_8_sd), .c(bindisplay_8_sc));  // open: dp
  not not_9 (not_9_out, SET_out);
  not not_10 (not_10_out, CLEAR_out);
  BinDisplay_VHDL bindisplay_vhdl_1 (
    .A(VQ3), .aa(bindisplay_vhdl_1_aa), .b(bindisplay_vhdl_1_b), .c(bindisplay_vhdl_1_c),
    .d(bindisplay_vhdl_1_d), .e(bindisplay_vhdl_1_e), .f(bindisplay_vhdl_1_f), .g(bindisplay_vhdl_1_g));
  _7_Segment_Display u_7_segment_display_10 (
    .g(bindisplay_vhdl_1_f), .f(bindisplay_vhdl_1_g), .a(bindisplay_vhdl_1_aa), .b(bindisplay_vhdl_1_b),
    .e(bindisplay_vhdl_1_e), .d(bindisplay_vhdl_1_d), .c(bindisplay_vhdl_1_c));  // open: dp
  Registrador_divisor_VHDL registrador_divisor_vhdl_1 (
    .set(not_9_out), .j(J), .clock(CLK), .p({S3, S2, S1, S0}), .clear(not_10_out), .Q({VQ3, VQ2, VQ1, VQ0}));
  BinDisplay_VHDL bindisplay_vhdl_2 (
    .A(VQ2), .aa(bindisplay_vhdl_2_aa), .b(bindisplay_vhdl_2_b), .c(bindisplay_vhdl_2_c),
    .d(bindisplay_vhdl_2_d), .e(bindisplay_vhdl_2_e), .f(bindisplay_vhdl_2_f), .g(bindisplay_vhdl_2_g));
  _7_Segment_Display u_7_segment_display_11 (
    .g(bindisplay_vhdl_2_f), .f(bindisplay_vhdl_2_g), .a(bindisplay_vhdl_2_aa), .b(bindisplay_vhdl_2_b),
    .e(bindisplay_vhdl_2_e), .d(bindisplay_vhdl_2_d), .c(bindisplay_vhdl_2_c));  // open: dp
  BinDisplay_VHDL bindisplay_vhdl_3 (
    .A(VQ1), .aa(bindisplay_vhdl_3_aa), .b(bindisplay_vhdl_3_b), .c(bindisplay_vhdl_3_c),
    .d(bindisplay_vhdl_3_d), .e(bindisplay_vhdl_3_e), .f(bindisplay_vhdl_3_f), .g(bindisplay_vhdl_3_g));
  _7_Segment_Display u_7_segment_display_12 (
    .g(bindisplay_vhdl_3_f), .f(bindisplay_vhdl_3_g), .a(bindisplay_vhdl_3_aa), .b(bindisplay_vhdl_3_b),
    .e(bindisplay_vhdl_3_e), .d(bindisplay_vhdl_3_d), .c(bindisplay_vhdl_3_c));  // open: dp
  BiHex_VHDL bihex_vhdl_1 (
    .A(VQ3), .B(VQ2), .C(VQ1), .D(VQ0), .aa(bihex_vhdl_1_aa), .bb(bihex_vhdl_1_bb), .cc(bihex_vhdl_1_cc),
    .dd(bihex_vhdl_1_dd), .e(bihex_vhdl_1_e), .f(bihex_vhdl_1_f), .g(bihex_vhdl_1_g));
  BinDisplay_VHDL bindisplay_vhdl_4 (
    .A(VQ0), .aa(bindisplay_vhdl_4_aa), .b(bindisplay_vhdl_4_b), .c(bindisplay_vhdl_4_c),
    .d(bindisplay_vhdl_4_d), .e(bindisplay_vhdl_4_e), .f(bindisplay_vhdl_4_f), .g(bindisplay_vhdl_4_g));
  _7_Segment_Display u_7_segment_display_13 (
    .g(bihex_vhdl_1_g), .f(bihex_vhdl_1_f), .a(bihex_vhdl_1_aa), .b(bihex_vhdl_1_bb), .e(bihex_vhdl_1_e),
    .d(bihex_vhdl_1_dd), .c(bihex_vhdl_1_cc));  // open: dp
  _7_Segment_Display u_7_segment_display_14 (
    .g(bindisplay_vhdl_4_f), .f(bindisplay_vhdl_4_g), .a(bindisplay_vhdl_4_aa), .b(bindisplay_vhdl_4_b),
    .e(bindisplay_vhdl_4_e), .d(bindisplay_vhdl_4_d), .c(bindisplay_vhdl_4_c));  // open: dp

  // Notes on the sheet:
  //   SAÍDA-PARELELA
  //   PRESET
  //   SAÍDA-SERIAL
  //   SAÍDA-PARALELA-VHDL
  //   SÁIDA-SERIAL-VHDL
endmodule

module Registrador_completo (
  input  S3,
  input  S2,
  input  S1,
  input  S0,
  input  C1,
  input  C0,
  input  J
);

  wire bihex_vhdl_1_aa, bihex_vhdl_1_bb, bihex_vhdl_1_cc, bihex_vhdl_1_dd, bihex_vhdl_1_e, bihex_vhdl_1_f,
       bihex_vhdl_1_g, bindisplay_1_sa, bindisplay_1_sb, bindisplay_1_sc, bindisplay_1_sd, bindisplay_1_se,
       bindisplay_1_sf, bindisplay_1_sg, bindisplay_2_sa, bindisplay_2_sb, bindisplay_2_sc, bindisplay_2_sd,
       bindisplay_2_se, bindisplay_2_sf, bindisplay_2_sg, bindisplay_3_sa, bindisplay_3_sb, bindisplay_3_sc,
       bindisplay_3_sd, bindisplay_3_se, bindisplay_3_sf, bindisplay_3_sg, bindisplay_4_sa, bindisplay_4_sb,
       bindisplay_4_sc, bindisplay_4_sd, bindisplay_4_se, bindisplay_4_sf, bindisplay_4_sg, bindisplay_5_sa,
       bindisplay_5_sb, bindisplay_5_sc, bindisplay_5_sd, bindisplay_5_se, bindisplay_5_sf, bindisplay_5_sg,
       bindisplay_6_sa, bindisplay_6_sb, bindisplay_6_sc, bindisplay_6_sd, bindisplay_6_se, bindisplay_6_sf,
       bindisplay_6_sg, bindisplay_7_sa, bindisplay_7_sb, bindisplay_7_sc, bindisplay_7_sd, bindisplay_7_se,
       bindisplay_7_sf, bindisplay_7_sg, bindisplay_8_sa, bindisplay_8_sb, bindisplay_8_sc, bindisplay_8_sd,
       bindisplay_8_se, bindisplay_8_sf, bindisplay_8_sg, bindisplay_9_sa, bindisplay_9_sb, bindisplay_9_sc,
       bindisplay_9_sd, bindisplay_9_se, bindisplay_9_sf, bindisplay_9_sg, bindisplay_10_sa,
       bindisplay_10_sb, bindisplay_10_sc, bindisplay_10_sd, bindisplay_10_se, bindisplay_10_sf,
       bindisplay_10_sg, bindisplay_11_sa, bindisplay_11_sb, bindisplay_11_sc, bindisplay_11_sd,
       bindisplay_11_se, bindisplay_11_sf, bindisplay_11_sg, bindisplay_vhdl_1_aa, bindisplay_vhdl_1_b,
       bindisplay_vhdl_1_c, bindisplay_vhdl_1_d, bindisplay_vhdl_1_e, bindisplay_vhdl_1_f,
       bindisplay_vhdl_1_g, bindisplay_vhdl_2_aa, bindisplay_vhdl_2_b, bindisplay_vhdl_2_c,
       bindisplay_vhdl_2_d, bindisplay_vhdl_2_e, bindisplay_vhdl_2_f, bindisplay_vhdl_2_g,
       bindisplay_vhdl_3_aa, bindisplay_vhdl_3_b, bindisplay_vhdl_3_c, bindisplay_vhdl_3_d,
       bindisplay_vhdl_3_e, bindisplay_vhdl_3_f, bindisplay_vhdl_3_g, bindisplay_vhdl_4_aa,
       bindisplay_vhdl_4_b, bindisplay_vhdl_4_c, bindisplay_vhdl_4_d, bindisplay_vhdl_4_e,
       bindisplay_vhdl_4_f, bindisplay_vhdl_4_g, CLEAR_out, COCK_out, conversor_1_a, conversor_1_b,
       conversor_1_c, conversor_1_d, conversor_1_e, conversor_1_f, conversor_1_g, mux2_1_out_7, mux2_2_out_7,
       mux2_3_out_7, mux2_4_out_7, not_1_out, not_2_out, Q0, Q1, Q2, Q3, VQ0, VQ1, VQ2, VQ3;

  BinDisplay bindisplay_1 (
    .A(J), .sa(bindisplay_1_sa), .sb(bindisplay_1_sb), .sc(bindisplay_1_sc), .sd(bindisplay_1_sd),
    .se(bindisplay_1_se), .sf(bindisplay_1_sf), .sg(bindisplay_1_sg));
  BinDisplay bindisplay_2 (
    .A(C1), .sa(bindisplay_2_sa), .sb(bindisplay_2_sb), .sc(bindisplay_2_sc), .sd(bindisplay_2_sd),
    .se(bindisplay_2_se), .sf(bindisplay_2_sf), .sg(bindisplay_2_sg));
  _7_Segment_Display u_7_segment_display_1 (
    .g(bindisplay_1_sf), .f(bindisplay_1_sg), .a(bindisplay_1_sa), .b(bindisplay_1_sb), .e(bindisplay_1_se),
    .d(bindisplay_1_sd), .c(bindisplay_1_sc));  // open: dp
  not not_1 (not_1_out, CLEAR_out);
  Button CLEAR (.out(CLEAR_out));
  _7_Segment_Display u_7_segment_display_2 (
    .g(bindisplay_2_sf), .f(bindisplay_2_sg), .a(bindisplay_2_sa), .b(bindisplay_2_sb), .e(bindisplay_2_se),
    .d(bindisplay_2_sd), .c(bindisplay_2_sc));  // open: dp
  Button COCK (.out(COCK_out));
  BinDisplay bindisplay_3 (
    .A(C0), .sa(bindisplay_3_sa), .sb(bindisplay_3_sb), .sc(bindisplay_3_sc), .sd(bindisplay_3_sd),
    .se(bindisplay_3_se), .sf(bindisplay_3_sf), .sg(bindisplay_3_sg));
  BinDisplay bindisplay_4 (
    .A(S3), .sa(bindisplay_4_sa), .sb(bindisplay_4_sb), .sc(bindisplay_4_sc), .sd(bindisplay_4_sd),
    .se(bindisplay_4_se), .sf(bindisplay_4_sf), .sg(bindisplay_4_sg));
  _7_Segment_Display u_7_segment_display_3 (
    .g(bindisplay_3_sf), .f(bindisplay_3_sg), .a(bindisplay_3_sa), .b(bindisplay_3_sb), .e(bindisplay_3_se),
    .d(bindisplay_3_sd), .c(bindisplay_3_sc));  // open: dp
  mux2 mux2_1 (.in_2(Q3), .in_4(Q2), .in_5(J), .in_6(S3), .C0(C0), .C1(C1), .out_7(mux2_1_out_7));
  _7_Segment_Display u_7_segment_display_4 (
    .g(bindisplay_4_sf), .f(bindisplay_4_sg), .a(bindisplay_4_sa), .b(bindisplay_4_sb), .e(bindisplay_4_se),
    .d(bindisplay_4_sd), .c(bindisplay_4_sc));  // open: dp
  BinDisplay bindisplay_5 (
    .A(Q3), .sa(bindisplay_5_sa), .sb(bindisplay_5_sb), .sc(bindisplay_5_sc), .sd(bindisplay_5_sd),
    .se(bindisplay_5_se), .sf(bindisplay_5_sf), .sg(bindisplay_5_sg));
  FFMEPSD ffmepsd_1 (.J(mux2_1_out_7), .SET(1'b1), .CLK(COCK_out), .CLEAR(not_1_out), .Q(Q3));  // open: NQ
  _7_Segment_Display u_7_segment_display_5 (
    .g(bindisplay_5_sf), .f(bindisplay_5_sg), .a(bindisplay_5_sa), .b(bindisplay_5_sb), .e(bindisplay_5_se),
    .d(bindisplay_5_sd), .c(bindisplay_5_sc));  // open: dp
  _7_Segment_Display u_7_segment_display_6 (
    .g(bindisplay_6_sf), .f(bindisplay_6_sg), .a(bindisplay_6_sa), .b(bindisplay_6_sb), .e(bindisplay_6_se),
    .d(bindisplay_6_sd), .c(bindisplay_6_sc));  // open: dp
  BinDisplay bindisplay_6 (
    .A(S2), .sa(bindisplay_6_sa), .sb(bindisplay_6_sb), .sc(bindisplay_6_sc), .sd(bindisplay_6_sd),
    .se(bindisplay_6_se), .sf(bindisplay_6_sf), .sg(bindisplay_6_sg));
  mux2 mux2_2 (.in_2(Q2), .in_4(Q1), .in_5(Q3), .in_6(S2), .C0(C0), .C1(C1), .out_7(mux2_2_out_7));
  BinDisplay bindisplay_7 (
    .A(Q2), .sa(bindisplay_7_sa), .sb(bindisplay_7_sb), .sc(bindisplay_7_sc), .sd(bindisplay_7_sd),
    .se(bindisplay_7_se), .sf(bindisplay_7_sf), .sg(bindisplay_7_sg));
  FFMEPSD ffmepsd_2 (.J(mux2_2_out_7), .SET(1'b1), .CLK(COCK_out), .CLEAR(not_1_out), .Q(Q2));  // open: NQ
  _7_Segment_Display u_7_segment_display_7 (
    .g(bindisplay_7_sf), .f(bindisplay_7_sg), .a(bindisplay_7_sa), .b(bindisplay_7_sb), .e(bindisplay_7_se),
    .d(bindisplay_7_sd), .c(bindisplay_7_sc));  // open: dp
  BinDisplay bindisplay_8 (
    .A(S1), .sa(bindisplay_8_sa), .sb(bindisplay_8_sb), .sc(bindisplay_8_sc), .sd(bindisplay_8_sd),
    .se(bindisplay_8_se), .sf(bindisplay_8_sf), .sg(bindisplay_8_sg));
  BinDisplay bindisplay_9 (
    .A(Q1), .sa(bindisplay_9_sa), .sb(bindisplay_9_sb), .sc(bindisplay_9_sc), .sd(bindisplay_9_sd),
    .se(bindisplay_9_se), .sf(bindisplay_9_sf), .sg(bindisplay_9_sg));
  _7_Segment_Display u_7_segment_display_8 (
    .g(bindisplay_8_sf), .f(bindisplay_8_sg), .a(bindisplay_8_sa), .b(bindisplay_8_sb), .e(bindisplay_8_se),
    .d(bindisplay_8_sd), .c(bindisplay_8_sc));  // open: dp
  _7_Segment_Display u_7_segment_display_9 (
    .g(bindisplay_9_sf), .f(bindisplay_9_sg), .a(bindisplay_9_sa), .b(bindisplay_9_sb), .e(bindisplay_9_se),
    .d(bindisplay_9_sd), .c(bindisplay_9_sc));  // open: dp
  mux2 mux2_3 (.in_2(Q1), .in_4(Q0), .in_5(Q2), .in_6(S1), .C0(C0), .C1(C1), .out_7(mux2_3_out_7));
  BinDisplay bindisplay_10 (
    .A(Q0), .sa(bindisplay_10_sa), .sb(bindisplay_10_sb), .sc(bindisplay_10_sc), .sd(bindisplay_10_sd),
    .se(bindisplay_10_se), .sf(bindisplay_10_sf), .sg(bindisplay_10_sg));
  FFMEPSD ffmepsd_3 (.J(mux2_3_out_7), .SET(1'b1), .CLK(COCK_out), .CLEAR(not_1_out), .Q(Q1));  // open: NQ
  BinDisplay bindisplay_11 (
    .A(S0), .sa(bindisplay_11_sa), .sb(bindisplay_11_sb), .sc(bindisplay_11_sc), .sd(bindisplay_11_sd),
    .se(bindisplay_11_se), .sf(bindisplay_11_sf), .sg(bindisplay_11_sg));
  _7_Segment_Display u_7_segment_display_10 (
    .g(bindisplay_10_sf), .f(bindisplay_10_sg), .a(bindisplay_10_sa), .b(bindisplay_10_sb),
    .e(bindisplay_10_se), .d(bindisplay_10_sd), .c(bindisplay_10_sc));  // open: dp
  _7_Segment_Display u_7_segment_display_11 (
    .g(bindisplay_11_sf), .f(bindisplay_11_sg), .a(bindisplay_11_sa), .b(bindisplay_11_sb),
    .e(bindisplay_11_se), .d(bindisplay_11_sd), .c(bindisplay_11_sc));  // open: dp
  conversor conversor_1 (
    .AA(Q3), .BB(Q2), .CC(Q1), .DD(Q0), .a(conversor_1_a), .b(conversor_1_b), .c(conversor_1_c),
    .d(conversor_1_d), .e(conversor_1_e), .f(conversor_1_f), .g(conversor_1_g));
  mux2 mux2_4 (.in_2(Q0), .in_4(J), .in_5(Q1), .in_6(S0), .C0(C0), .C1(C1), .out_7(mux2_4_out_7));
  FFMEPSD ffmepsd_4 (.J(mux2_4_out_7), .SET(1'b1), .CLK(COCK_out), .CLEAR(not_1_out), .Q(Q0));  // open: NQ
  _7_Segment_Display u_7_segment_display_12 (
    .g(conversor_1_g), .f(conversor_1_f), .a(conversor_1_a), .b(conversor_1_b), .e(conversor_1_e),
    .d(conversor_1_d), .c(conversor_1_c));  // open: dp
  not not_2 (not_2_out, not_1_out);
  BinDisplay_VHDL bindisplay_vhdl_1 (
    .A(VQ3), .aa(bindisplay_vhdl_1_aa), .b(bindisplay_vhdl_1_b), .c(bindisplay_vhdl_1_c),
    .d(bindisplay_vhdl_1_d), .e(bindisplay_vhdl_1_e), .f(bindisplay_vhdl_1_f), .g(bindisplay_vhdl_1_g));
  Registrador_completo_VHDL registrador_completo_vhdl_1 (
    .sel({C1, C0}), .j(J), .clock(COCK_out), .p({S3, S2, S1, S0}), .clear(not_2_out), .Q({VQ3, VQ2, VQ1, VQ0}));
  _7_Segment_Display u_7_segment_display_13 (
    .g(bindisplay_vhdl_1_f), .f(bindisplay_vhdl_1_g), .a(bindisplay_vhdl_1_aa), .b(bindisplay_vhdl_1_b),
    .e(bindisplay_vhdl_1_e), .d(bindisplay_vhdl_1_d), .c(bindisplay_vhdl_1_c));  // open: dp
  BinDisplay_VHDL bindisplay_vhdl_2 (
    .A(VQ2), .aa(bindisplay_vhdl_2_aa), .b(bindisplay_vhdl_2_b), .c(bindisplay_vhdl_2_c),
    .d(bindisplay_vhdl_2_d), .e(bindisplay_vhdl_2_e), .f(bindisplay_vhdl_2_f), .g(bindisplay_vhdl_2_g));
  _7_Segment_Display u_7_segment_display_14 (
    .g(bindisplay_vhdl_2_f), .f(bindisplay_vhdl_2_g), .a(bindisplay_vhdl_2_aa), .b(bindisplay_vhdl_2_b),
    .e(bindisplay_vhdl_2_e), .d(bindisplay_vhdl_2_d), .c(bindisplay_vhdl_2_c));  // open: dp
  BinDisplay_VHDL bindisplay_vhdl_3 (
    .A(VQ1), .aa(bindisplay_vhdl_3_aa), .b(bindisplay_vhdl_3_b), .c(bindisplay_vhdl_3_c),
    .d(bindisplay_vhdl_3_d), .e(bindisplay_vhdl_3_e), .f(bindisplay_vhdl_3_f), .g(bindisplay_vhdl_3_g));
  BiHex_VHDL bihex_vhdl_1 (
    .A(VQ3), .B(VQ2), .C(VQ1), .D(VQ0), .aa(bihex_vhdl_1_aa), .bb(bihex_vhdl_1_bb), .cc(bihex_vhdl_1_cc),
    .dd(bihex_vhdl_1_dd), .e(bihex_vhdl_1_e), .f(bihex_vhdl_1_f), .g(bihex_vhdl_1_g));
  _7_Segment_Display u_7_segment_display_15 (
    .g(bindisplay_vhdl_3_f), .f(bindisplay_vhdl_3_g), .a(bindisplay_vhdl_3_aa), .b(bindisplay_vhdl_3_b),
    .e(bindisplay_vhdl_3_e), .d(bindisplay_vhdl_3_d), .c(bindisplay_vhdl_3_c));  // open: dp
  _7_Segment_Display u_7_segment_display_16 (
    .g(bihex_vhdl_1_g), .f(bihex_vhdl_1_f), .a(bihex_vhdl_1_aa), .b(bihex_vhdl_1_bb), .e(bihex_vhdl_1_e),
    .d(bihex_vhdl_1_dd), .c(bihex_vhdl_1_cc));  // open: dp
  BinDisplay_VHDL bindisplay_vhdl_4 (
    .A(VQ0), .aa(bindisplay_vhdl_4_aa), .b(bindisplay_vhdl_4_b), .c(bindisplay_vhdl_4_c),
    .d(bindisplay_vhdl_4_d), .e(bindisplay_vhdl_4_e), .f(bindisplay_vhdl_4_f), .g(bindisplay_vhdl_4_g));
  _7_Segment_Display u_7_segment_display_17 (
    .g(bindisplay_vhdl_4_f), .f(bindisplay_vhdl_4_g), .a(bindisplay_vhdl_4_aa), .b(bindisplay_vhdl_4_b),
    .e(bindisplay_vhdl_4_e), .d(bindisplay_vhdl_4_d), .c(bindisplay_vhdl_4_c));  // open: dp

  // Notes on the sheet:
  //   SELETOR
  //   PRESET
  //   SAÍDA-PARELELA
  //   SAÍDA-SERIAL
  //   SAÍDA-PARALELA-VHDL
  //   SÁIDA-SERIAL-VHDL
endmodule

module Registrador_multiplicador (
  input  S3,
  input  S0,
  input  S1,
  input  S2,
  input  J,
  input  CLK,
  output [3:0] out_7
);

  wire and_1_out, and_2_out, and_3_out, and_4_out, and_5_out, and_6_out, and_7_out, and_8_out,
       bindisplay_1_sa, bindisplay_1_sb, bindisplay_1_sc, bindisplay_1_sd, bindisplay_1_se, bindisplay_1_sf,
       bindisplay_1_sg, bindisplay_2_sa, bindisplay_2_sb, bindisplay_2_sc, bindisplay_2_sd, bindisplay_2_se,
       bindisplay_2_sf, bindisplay_2_sg, bindisplay_3_sa, bindisplay_3_sb, bindisplay_3_sc, bindisplay_3_sd,
       bindisplay_3_se, bindisplay_3_sf, bindisplay_3_sg, bindisplay_4_sa, bindisplay_4_sb, bindisplay_4_sc,
       bindisplay_4_sd, bindisplay_4_se, bindisplay_4_sf, bindisplay_4_sg, bindisplay_5_sa, bindisplay_5_sb,
       bindisplay_5_sc, bindisplay_5_sd, bindisplay_5_se, bindisplay_5_sf, bindisplay_5_sg, bindisplay_6_sa,
       bindisplay_6_sb, bindisplay_6_sc, bindisplay_6_sd, bindisplay_6_se, bindisplay_6_sf, bindisplay_6_sg,
       bindisplay_7_sa, bindisplay_7_sb, bindisplay_7_sc, bindisplay_7_sd, bindisplay_7_se, bindisplay_7_sf,
       bindisplay_7_sg, bindisplay_8_sa, bindisplay_8_sb, bindisplay_8_sc, bindisplay_8_sd, bindisplay_8_se,
       bindisplay_8_sf, bindisplay_8_sg, bindisplay_9_sa, bindisplay_9_sb, bindisplay_9_sc, bindisplay_9_sd,
       bindisplay_9_se, bindisplay_9_sf, bindisplay_9_sg, bindisplay_10_sa, bindisplay_10_sb,
       bindisplay_10_sc, bindisplay_10_sd, bindisplay_10_se, bindisplay_10_sf, bindisplay_10_sg,
       bindisplay_11_sa, bindisplay_11_sb, bindisplay_11_sc, bindisplay_11_sd, bindisplay_11_se,
       bindisplay_11_sf, bindisplay_11_sg, bindisplay_12_sa, bindisplay_12_sb, bindisplay_12_sc,
       bindisplay_12_sd, bindisplay_12_se, bindisplay_12_sf, bindisplay_12_sg, CLEAR_out, conversor_1_a,
       conversor_1_b, conversor_1_c, conversor_1_d, conversor_1_e, conversor_1_f, conversor_1_g,
       conversor_2_a, conversor_2_b, conversor_2_c, conversor_2_d, conversor_2_e, conversor_2_f,
       conversor_2_g, not_1_out, not_2_out, not_3_out, not_4_out, not_5_out, not_6_out, not_7_out, not_8_out,
       not_9_out, not_10_out, or_1_out, or_2_out, or_3_out, or_4_out, Q0, Q1, Q2, Q3, SET_out;

  BinDisplay bindisplay_1 (
    .A(Q0), .sa(bindisplay_1_sa), .sb(bindisplay_1_sb), .sc(bindisplay_1_sc), .sd(bindisplay_1_sd),
    .se(bindisplay_1_se), .sf(bindisplay_1_sf), .sg(bindisplay_1_sg));
  _7_Segment_Display u_7_segment_display_1 (
    .g(bindisplay_1_sf), .f(bindisplay_1_sg), .a(bindisplay_1_sa), .b(bindisplay_1_sb), .e(bindisplay_1_se),
    .d(bindisplay_1_sd), .c(bindisplay_1_sc));  // open: dp
  Button SET (.out(SET_out));
  Button CLEAR (.out(CLEAR_out));
  BinDisplay bindisplay_2 (
    .A(Q1), .sa(bindisplay_2_sa), .sb(bindisplay_2_sb), .sc(bindisplay_2_sc), .sd(bindisplay_2_sd),
    .se(bindisplay_2_se), .sf(bindisplay_2_sf), .sg(bindisplay_2_sg));
  BinDisplay bindisplay_3 (
    .A(S0), .sa(bindisplay_3_sa), .sb(bindisplay_3_sb), .sc(bindisplay_3_sc), .sd(bindisplay_3_sd),
    .se(bindisplay_3_se), .sf(bindisplay_3_sf), .sg(bindisplay_3_sg));
  _7_Segment_Display u_7_segment_display_2 (
    .g(bindisplay_2_sf), .f(bindisplay_2_sg), .a(bindisplay_2_sa), .b(bindisplay_2_sb), .e(bindisplay_2_se),
    .d(bindisplay_2_sd), .c(bindisplay_2_sc));  // open: dp
  and and_1 (and_1_out, SET_out, S0);
  not not_1 (not_1_out, and_1_out);
  and and_2 (and_2_out, ~S0, SET_out);  // AND_Gate
  or or_1 (or_1_out, and_2_out, CLEAR_out);
  not not_2 (not_2_out, or_1_out);
  _7_Segment_Display u_7_segment_display_3 (
    .g(bindisplay_3_sf), .f(bindisplay_3_sg), .a(bindisplay_3_sa), .b(bindisplay_3_sb), .e(bindisplay_3_se),
    .d(bindisplay_3_sd), .c(bindisplay_3_sc));  // open: dp
  FFMEPSD ffmepsd_1 (.J(Q1), .SET(not_1_out), .CLK(CLK), .CLEAR(not_2_out), .Q(Q0));  // open: NQ
  BinDisplay bindisplay_4 (
    .A(Q2), .sa(bindisplay_4_sa), .sb(bindisplay_4_sb), .sc(bindisplay_4_sc), .sd(bindisplay_4_sd),
    .se(bindisplay_4_se), .sf(bindisplay_4_sf), .sg(bindisplay_4_sg));
  and and_3 (and_3_out, SET_out, S1);
  not not_3 (not_3_out, and_3_out);
  and and_4 (and_4_out, ~S1, SET_out);  // AND_Gate
  or or_2 (or_2_out, and_4_out, CLEAR_out);
  not not_4 (not_4_out, or_2_out);
  BinDisplay bindisplay_5 (
    .A(S1), .sa(bindisplay_5_sa), .sb(bindisplay_5_sb), .sc(bindisplay_5_sc), .sd(bindisplay_5_sd),
    .se(bindisplay_5_se), .sf(bindisplay_5_sf), .sg(bindisplay_5_sg));
  _7_Segment_Display u_7_segment_display_4 (
    .g(bindisplay_4_sf), .f(bindisplay_4_sg), .a(bindisplay_4_sa), .b(bindisplay_4_sb), .e(bindisplay_4_se),
    .d(bindisplay_4_sd), .c(bindisplay_4_sc));  // open: dp
  FFMEPSD ffmepsd_2 (.J(Q2), .SET(not_3_out), .CLK(CLK), .CLEAR(not_4_out), .Q(Q1));  // open: NQ
  and and_5 (and_5_out, ~S2, SET_out);  // AND_Gate
  _7_Segment_Display u_7_segment_display_5 (
    .g(bindisplay_5_sf), .f(bindisplay_5_sg), .a(bindisplay_5_sa), .b(bindisplay_5_sb), .e(bindisplay_5_se),
    .d(bindisplay_5_sd), .c(bindisplay_5_sc));  // open: dp
  BinDisplay bindisplay_6 (
    .A(Q3), .sa(bindisplay_6_sa), .sb(bindisplay_6_sb), .sc(bindisplay_6_sc), .sd(bindisplay_6_sd),
    .se(bindisplay_6_se), .sf(bindisplay_6_sf), .sg(bindisplay_6_sg));
  and and_6 (and_6_out, SET_out, S2);
  not not_5 (not_5_out, and_6_out);
  or or_3 (or_3_out, and_5_out, CLEAR_out);
  not not_6 (not_6_out, or_3_out);
  BinDisplay bindisplay_7 (
    .A(S2), .sa(bindisplay_7_sa), .sb(bindisplay_7_sb), .sc(bindisplay_7_sc), .sd(bindisplay_7_sd),
    .se(bindisplay_7_se), .sf(bindisplay_7_sf), .sg(bindisplay_7_sg));
  _7_Segment_Display u_7_segment_display_6 (
    .g(bindisplay_6_sf), .f(bindisplay_6_sg), .a(bindisplay_6_sa), .b(bindisplay_6_sb), .e(bindisplay_6_se),
    .d(bindisplay_6_sd), .c(bindisplay_6_sc));  // open: dp
  FFMEPSD ffmepsd_3 (.J(Q3), .SET(not_5_out), .CLK(CLK), .CLEAR(not_6_out), .Q(Q2));  // open: NQ
  and and_7 (and_7_out, ~S3, SET_out);  // AND_Gate
  _7_Segment_Display u_7_segment_display_7 (
    .g(bindisplay_7_sf), .f(bindisplay_7_sg), .a(bindisplay_7_sa), .b(bindisplay_7_sb), .e(bindisplay_7_se),
    .d(bindisplay_7_sd), .c(bindisplay_7_sc));  // open: dp
  and and_8 (and_8_out, SET_out, S3);
  not not_7 (not_7_out, and_8_out);
  FFMEPSD ffmepsd_4 (.J(J), .SET(not_7_out), .CLK(CLK), .CLEAR(not_8_out), .Q(Q3));  // open: NQ
  or or_4 (or_4_out, and_7_out, CLEAR_out);
  not not_8 (not_8_out, or_4_out);
  BinDisplay bindisplay_8 (
    .A(S3), .sa(bindisplay_8_sa), .sb(bindisplay_8_sb), .sc(bindisplay_8_sc), .sd(bindisplay_8_sd),
    .se(bindisplay_8_se), .sf(bindisplay_8_sf), .sg(bindisplay_8_sg));
  _7_Segment_Display u_7_segment_display_8 (
    .g(bindisplay_8_sf), .f(bindisplay_8_sg), .a(bindisplay_8_sa), .b(bindisplay_8_sb), .e(bindisplay_8_se),
    .d(bindisplay_8_sd), .c(bindisplay_8_sc));  // open: dp
  conversor conversor_1 (
    .AA(Q0), .BB(Q1), .CC(Q2), .DD(Q3), .a(conversor_1_a), .b(conversor_1_b), .c(conversor_1_c),
    .d(conversor_1_d), .e(conversor_1_e), .f(conversor_1_f), .g(conversor_1_g));
  not not_9 (not_9_out, SET_out);
  not not_10 (not_10_out, CLEAR_out);
  _7_Segment_Display u_7_segment_display_9 (
    .g(conversor_1_g), .f(conversor_1_f), .a(conversor_1_a), .b(conversor_1_b), .e(conversor_1_e),
    .d(conversor_1_d), .c(conversor_1_c));  // open: dp
  BinDisplay bindisplay_9 (
    .A(out_7[3]), .sa(bindisplay_9_sa), .sb(bindisplay_9_sb), .sc(bindisplay_9_sc), .sd(bindisplay_9_sd),
    .se(bindisplay_9_se), .sf(bindisplay_9_sf), .sg(bindisplay_9_sg));
  Registrador_multiplicador_VHDL registrador_multiplicador_vhdl_1 (
    .set(not_9_out), .j(J), .clock(CLK), .p({S3, S2, S1, S0}), .clear(not_10_out), .Q(out_7));
  _7_Segment_Display u_7_segment_display_10 (
    .g(bindisplay_9_sf), .f(bindisplay_9_sg), .a(bindisplay_9_sa), .b(bindisplay_9_sb), .e(bindisplay_9_se),
    .d(bindisplay_9_sd), .c(bindisplay_9_sc));  // open: dp
  BinDisplay bindisplay_10 (
    .A(out_7[2]), .sa(bindisplay_10_sa), .sb(bindisplay_10_sb), .sc(bindisplay_10_sc), .sd(bindisplay_10_sd),
    .se(bindisplay_10_se), .sf(bindisplay_10_sf), .sg(bindisplay_10_sg));
  conversor conversor_2 (
    .AA(out_7[3]), .BB(out_7[2]), .CC(out_7[1]), .DD(out_7[0]), .a(conversor_2_a), .b(conversor_2_b),
    .c(conversor_2_c), .d(conversor_2_d), .e(conversor_2_e), .f(conversor_2_f), .g(conversor_2_g));
  _7_Segment_Display u_7_segment_display_11 (
    .g(bindisplay_10_sf), .f(bindisplay_10_sg), .a(bindisplay_10_sa), .b(bindisplay_10_sb),
    .e(bindisplay_10_se), .d(bindisplay_10_sd), .c(bindisplay_10_sc));  // open: dp
  _7_Segment_Display u_7_segment_display_12 (
    .g(conversor_2_g), .f(conversor_2_f), .a(conversor_2_a), .b(conversor_2_b), .e(conversor_2_e),
    .d(conversor_2_d), .c(conversor_2_c));  // open: dp
  BinDisplay bindisplay_11 (
    .A(out_7[1]), .sa(bindisplay_11_sa), .sb(bindisplay_11_sb), .sc(bindisplay_11_sc), .sd(bindisplay_11_sd),
    .se(bindisplay_11_se), .sf(bindisplay_11_sf), .sg(bindisplay_11_sg));
  _7_Segment_Display u_7_segment_display_13 (
    .g(bindisplay_11_sf), .f(bindisplay_11_sg), .a(bindisplay_11_sa), .b(bindisplay_11_sb),
    .e(bindisplay_11_se), .d(bindisplay_11_sd), .c(bindisplay_11_sc));  // open: dp
  BinDisplay bindisplay_12 (
    .A(out_7[0]), .sa(bindisplay_12_sa), .sb(bindisplay_12_sb), .sc(bindisplay_12_sc), .sd(bindisplay_12_sd),
    .se(bindisplay_12_se), .sf(bindisplay_12_sf), .sg(bindisplay_12_sg));
  _7_Segment_Display u_7_segment_display_14 (
    .g(bindisplay_12_sf), .f(bindisplay_12_sg), .a(bindisplay_12_sa), .b(bindisplay_12_sb),
    .e(bindisplay_12_se), .d(bindisplay_12_sd), .c(bindisplay_12_sc));  // open: dp

  // Other names for the same wires on the sheet: VQ0 = out_7[0]; VQ1 = out_7[1]; VQ2 = out_7[2]; VQ3 = out_7[3]

  // Notes on the sheet:
  //   SAÍDA-PARELELA
  //   PRESET
  //   SAÍDA-SERIAL
  //   SÁIDA-SERIAL-VHDL
  //   SAÍDA-PARALELA-VHDL
endmodule

module JKME (
  input  SET,
  input  J,
  input  COCK,
  input  K,
  input  RESET,
  output Q,
  output NQ
);

  wire nand_1_out, nand_2_out, nand_3_out, nand_4_out, nand_5_out, nand_6_out, not_1_out;

  nand nand_1 (nand_1_out, COCK, J, NQ);
  nand nand_2 (nand_2_out, Q, K, COCK);
  not not_1 (not_1_out, COCK);
  nand nand_3 (nand_3_out, SET, nand_1_out, nand_4_out);
  nand nand_4 (nand_4_out, nand_3_out, nand_2_out, RESET);
  nand nand_5 (nand_5_out, nand_3_out, not_1_out);
  nand nand_6 (nand_6_out, not_1_out, nand_4_out);
  nand nand_7 (Q, SET, nand_5_out, NQ);
  nand nand_8 (NQ, Q, nand_6_out, RESET);
endmodule

module FFT (
  input  SET,
  input  J,
  input  clk,
  input  CLEAR,
  output Q,
  output NQ
);

  JKME jkme_1 (.SET(SET), .J(J), .COCK(clk), .K(J), .RESET(CLEAR), .Q(Q), .NQ(NQ));
endmodule

// D
module FFMEPSD (
  input  SET,
  input  J,
  input  CLK,
  input  CLEAR,
  output Q,
  output NQ
);

  wire not_1_out;

  not not_1 (not_1_out, J);
  JKME jkme_1 (.SET(SET), .J(J), .COCK(CLK), .K(not_1_out), .RESET(CLEAR), .Q(Q), .NQ(NQ));
endmodule

module mux (
  input  Entrada1,
  input  Entrada2,
  input  sel,
  output out_4
);

  wire and_1_out, and_2_out;

  and and_1 (and_1_out, Entrada1, ~sel);  // AND_Gate
  and and_2 (and_2_out, Entrada2, sel);
  or or_1 (out_4, and_1_out, and_2_out);
endmodule

// MUX
module mux2 (
  input  C0,
  input  in_2,
  input  C1,
  input  in_4,
  input  in_5,
  input  in_6,
  output out_7
);

  wire mux_1_out_4, mux_2_out_4;

  mux mux_1 (.Entrada1(in_2), .Entrada2(in_4), .sel(C0), .out_4(mux_1_out_4));
  mux mux_2 (.Entrada1(in_5), .Entrada2(in_6), .sel(C0), .out_4(mux_2_out_4));
  mux mux_3 (.Entrada1(mux_1_out_4), .Entrada2(mux_2_out_4), .sel(C1), .out_4(out_7));
endmodule

module conversor (
  input  AA,
  input  BB,
  input  CC,
  input  DD,
  output a,
  output b,
  output c,
  output d,
  output e,
  output f,
  output g
);

  wire and_1_out, and_2_out, and_3_out, and_4_out, and_5_out, and_6_out, and_7_out, and_8_out, and_9_out,
       and_10_out, and_11_out, and_12_out, and_13_out, and_14_out, and_15_out, and_16_out, and_17_out,
       and_18_out, and_19_out, and_20_out, and_21_out, and_22_out, and_23_out, and_24_out, and_25_out,
       and_26_out, and_27_out, and_28_out, and_29_out, and_30_out, and_31_out, and_32_out, and_33_out,
       and_34_out, and_35_out, not_1_out, not_2_out, not_3_out, not_4_out;

  not not_1 (not_1_out, AA);
  not not_2 (not_2_out, BB);
  not not_3 (not_3_out, CC);
  not not_4 (not_4_out, DD);
  and and_1 (and_1_out, not_2_out, not_4_out);
  and and_2 (and_2_out, not_1_out, CC);
  and and_3 (and_3_out, not_1_out, BB, DD);
  and and_4 (and_4_out, AA, not_2_out, not_3_out);
  and and_5 (and_5_out, AA, not_4_out);
  and and_6 (and_6_out, BB, CC);
  and and_7 (and_7_out, not_1_out, not_3_out, not_4_out);
  and and_8 (and_8_out, not_1_out, CC, DD);
  and and_9 (and_9_out, not_2_out, not_4_out);
  and and_10 (and_10_out, AA, not_3_out, DD);
  and and_11 (and_11_out, not_1_out, not_2_out);
  and and_12 (and_12_out, not_1_out, BB);
  and and_13 (and_13_out, AA, not_2_out);
  and and_14 (and_14_out, not_3_out, DD);
  and and_15 (and_15_out, not_2_out, not_3_out);
  and and_16 (and_16_out, not_2_out, DD);
  and and_17 (and_17_out, BB, not_3_out, DD);
  and and_18 (and_18_out, not_1_out, not_2_out, not_4_out);
  and and_19 (and_19_out, not_2_out, CC, DD);
  and and_20 (and_20_out, AA, not_3_out);
  and and_21 (and_21_out, BB, CC, not_4_out);
  and and_22 (and_22_out, not_2_out, not_4_out);
  and and_23 (and_23_out, CC, not_4_out);
  and and_24 (and_24_out, AA, CC);
  and and_25 (and_25_out, AA, BB);
  and and_26 (and_26_out, not_3_out, not_4_out);
  and and_27 (and_27_out, not_1_out, BB, not_3_out);
  and and_28 (and_28_out, BB, not_4_out);
  and and_29 (and_29_out, AA, not_2_out);
  and and_30 (and_30_out, AA, CC);
  and and_31 (and_31_out, not_2_out, CC);
  and and_32 (and_32_out, AA, not_2_out);
  and and_33 (and_33_out, not_1_out, BB, not_3_out);
  and and_34 (and_34_out, CC, not_4_out);
  and and_35 (and_35_out, AA, DD);
  or or_1 (a, and_1_out, and_2_out, and_3_out, and_4_out, and_5_out, and_6_out);
  or or_2 (b, and_7_out, and_8_out, and_9_out, and_10_out, and_11_out);
  or or_3 (c, and_12_out, and_13_out, and_14_out, and_15_out, and_16_out);
  or or_4 (d, and_17_out, and_18_out, and_19_out, and_20_out, and_21_out);
  or or_5 (e, and_22_out, and_23_out, and_24_out, and_25_out);
  or or_6 (f, and_26_out, and_27_out, and_28_out, and_29_out, and_30_out);
  or or_7 (g, and_31_out, and_32_out, and_33_out, and_34_out, and_35_out);
endmodule

module BinDisplay (
  input  A,
  output sa,
  output sb,
  output sc,
  output sd,
  output se,
  output sf,
  output sg
);

  not not_1 (sa, A);

  assign sb = 1'b1;
  assign sc = 1'b1;
  assign sd = sa;
  assign se = sa;
  assign sf = 1'b0;
  assign sg = sa;
endmodule

// VHDL entity Registrador_completo_VHDL, as the project stores it:
LIBRARY ieee;
USE ieee.std_logic_1164.all;

ENTITY Registrador_completo_VHDL IS
  PORT (
  ------------------------------------------------------------------------------
    sel      : IN  std_logic_vector(1 DOWNTO 0);  -- Select mode                  
    j        : IN  std_logic;                    -- Input for shift operations
    clock    : IN std_logic;                     -- Clock signal
    p        : IN std_logic_vector(3 downto 0);               -- Parallel inputs
    clear    : IN std_logic;                     -- Asynchronous clear
  ------------------------------------------------------------------------------
    Q        : OUT std_logic_vector(3 DOWNTO 0)  -- Outputs
  ------------------------------------------------------------------------------
  );
END Registrador_completo_VHDL;

ARCHITECTURE TypeArchitecture OF Registrador_completo_VHDL IS
    signal REG : STD_LOGIC_VECTOR(3 DOWNTO 0) := "0000";
BEGIN
    PROCESS(clock, clear)
    BEGIN
        IF clear = '1' THEN
            REG <= "0000"; 

        ELSIF falling_edge(clock) THEN
            CASE sel IS
                WHEN "00" =>
                    REG <= REG;
                WHEN "01" =>
                    REG <= REG(2 DOWNTO 0) & j;
                WHEN "10" =>
                	REG <= j & REG(3 DOWNTO 1);
                    
                WHEN "11" =>
                    REG <= p;
                    
                WHEN OTHERS =>
                    REG <= REG;  -- Default case
            END CASE;
        END IF;
    END PROCESS;

    Q <= REG;

END TypeArchitecture;

// VHDL entity jk_mestre_escravo, as the project stores it:
library IEEE;
use IEEE.STD_LOGIC_1164.ALL;

entity jk_mestre_escravo is
    Port (
        J      : in STD_LOGIC;       
        K      : in STD_LOGIC;        
        CLK    : in STD_LOGIC;        
        PRESET : in STD_LOGIC;        
        CLEAR  : in STD_LOGIC;       
        Q      : out STD_LOGIC;      
        QN     : out STD_LOGIC        
    );
end jk_mestre_escravo;

architecture Behavioral of jk_mestre_escravo is
    signal master_q : STD_LOGIC := '0'; 
begin
    process(CLK, PRESET, CLEAR)
    begin

        if (CLEAR = '0') then
            master_q <= '0';
        elsif (PRESET = '0') then
            master_q <= '1';
        elsif rising_edge(CLK) then

            if (J = '0' and K = '1') then
                master_q <= '0'; 
            elsif (J = '1' and K = '0') then
                master_q <= '1'; 
            elsif (J = '1' and K = '1') then
                master_q <= NOT master_q; 
            end if;
        end if;
    end process;


    process(CLK, PRESET, CLEAR)
    begin

        if (CLEAR = '0') then
            Q <= '0';
            QN <= '1';
        elsif (PRESET = '0') then
            Q <= '1';
            QN <= '0';
        elsif falling_edge(CLK) then

            Q <= master_q;
            QN <= NOT master_q;
        end if;
    end process;
end Behavioral;

// VHDL entity MUX2_VHDL, as the project stores it:
--------------------------------------------------------------------------------
-- Project :
-- File    :
-- Autor   :
-- Date    :
--
--------------------------------------------------------------------------------
-- Description :
--
--------------------------------------------------------------------------------

LIBRARY ieee;
USE ieee.std_logic_1164.all;

ENTITY MUX2_VHDL IS
  PORT (
  ------------------------------------------------------------------------------
  --Insert input ports below
    sel      : IN  std_logic_vector(1 downto 0);               
    A        : IN  std_logic;
    B        : IN  std_logic;
    C        : IN  std_logic;
    D        : IN  std_logic;
  ------------------------------------------------------------------------------
  --Insert output ports below
    RES        : OUT std_logic            
    );
END MUX2_VHDL;

--------------------------------------------------------------------------------
--Complete your VHDL description below
--------------------------------------------------------------------------------

ARCHITECTURE TypeArchitecture OF MUX2_VHDL IS

BEGIN
	process (sel,A,B,C,D)
	BEGIN
		IF SEL = "00" THEN
			RES <= A;
		ELSIF SEL = "01" THEN
			RES <= B;
		ELSIF SEL = "10" THEN
			RES <= C;
		ELSIF SEL = "11" THEN
			RES <= D;
		END IF;
	END PROCESS;
			

END TypeArchitecture;

// VHDL entity Registrador_divisor_VHDL, as the project stores it:
LIBRARY ieee;
USE ieee.std_logic_1164.all;

ENTITY Registrador_divisor_VHDL IS
  PORT (
  ------------------------------------------------------------------------------
    set      : IN  std_logic;  -- Select mode                  
    j        : IN  std_logic;                    -- Input for shift operations
    clock    : IN std_logic;                     -- Clock signal
    p        : IN std_logic_vector(3 downto 0);               -- Parallel inputs
    clear    : IN std_logic;                     -- Asynchronous clear
  ------------------------------------------------------------------------------
    Q        : OUT std_logic_vector(3 DOWNTO 0)  -- Outputs
  ------------------------------------------------------------------------------
  );
END Registrador_divisor_VHDL;

ARCHITECTURE TypeArchitecture OF Registrador_divisor_VHDL IS
    signal REG : STD_LOGIC_VECTOR(3 DOWNTO 0) := "0000";
BEGIN
    PROCESS(clock, clear, set)
    BEGIN
        IF clear = '0' THEN
            REG <= "0000"; 
        elsif set = '0' then
            REG <= P(3) & P(2) & P(1) & P(0);
        ELSIF falling_edge(clock) THEN
               REG <= j & REG(3 DOWNTO 1);
        END IF;
    END PROCESS;

    Q <= REG;

END TypeArchitecture;

// VHDL entity Divisor_freq_VHDL, as the project stores it:
LIBRARY ieee;
USE ieee.std_logic_1164.all;
USE ieee.numeric_std.all;

ENTITY Divisor_freq_VHDL IS
  PORT (
  ------------------------------------------------------------------------------
  --Insert input ports below
    SET        : IN std_logic;	
    CLOCK      : IN  std_logic;                    -- input bit example
    J        : IN  std_logic; -- input vector example
    CLEAR      : IN STD_LOGIC;
    S		: OUT  std_logic_vector(3 DOWNTO 0)
    );
END Divisor_freq_VHDL;


ARCHITECTURE TypeArchitecture OF Divisor_freq_VHDL IS
	signal AUX_S : STD_LOGIC_VECTOR(3 DOWNTO 0) := "0000"; 
BEGIN
	PROCESS(J, CLOCK, CLEAR, SET)
	BEGIN
		IF CLEAR = '0' THEN
			AUX_S <= "0000";
		ELSIF SET = '0' THEN
			AUX_S <= "1111";
		ELSIF FALLING_EDGE(CLOCK) and (J = '1') THEN
			AUX_S <= std_logic_vector(unsigned(AUX_S) + 1);
	END IF;
	END PROCESS;

	S <= AUX_S;

END TypeArchitecture;

// VHDL entity Registrador_multiplicador_VHDL, as the project stores it:
LIBRARY ieee;
USE ieee.std_logic_1164.all;

ENTITY Registrador_multiplicador_VHDL IS
  PORT (
  ------------------------------------------------------------------------------
    set      : IN  std_logic;  -- Select mode                  
    j        : IN  std_logic;                    -- Input for shift operations
    clock    : IN std_logic;                     -- Clock signal
    p        : IN std_logic_vector(3 downto 0);               -- Parallel inputs
    clear    : IN std_logic;                     -- Asynchronous clear
  ------------------------------------------------------------------------------
    Q        : OUT std_logic_vector(3 DOWNTO 0)  -- Outputs
  ------------------------------------------------------------------------------
  );
END Registrador_multiplicador_VHDL;

ARCHITECTURE TypeArchitecture OF Registrador_multiplicador_VHDL IS
    signal REG : STD_LOGIC_VECTOR(3 DOWNTO 0) := "0000";
BEGIN
    PROCESS(clock, clear, set)
    BEGIN
        IF clear = '0' THEN
            REG <= "0000"; 
        elsif set = '0' then
            REG <= P(3) & P(2) & P(1) & P(0);
        ELSIF falling_edge(clock) THEN
               REG <= REG(2 DOWNTO 0) & j;
        END IF;
    END PROCESS;

    Q <= REG;

END TypeArchitecture;

// VHDL entity divisor_freq_VHDL_bruto, as the project stores it:
library IEEE;
use IEEE.STD_LOGIC_1164.ALL;

entity divisor_freq_VHDL_bruto is
    Port (
        T      : in STD_LOGIC;        CLK    : in STD_LOGIC;
        PRESET : in STD_LOGIC;
        CLEAR  : in STD_LOGIC;
        Q1     : out STD_LOGIC;
        Q1N    : out STD_LOGIC;
        Q2     : out STD_LOGIC;
        Q2N    : out STD_LOGIC;
        Q3     : out STD_LOGIC;
        Q3N    : out STD_LOGIC;
        Q4     : out STD_LOGIC;
        Q4N    : out STD_LOGIC
    );
end divisor_freq_VHDL_bruto;

architecture Behavioral of divisor_freq_VHDL_bruto is
    signal ff1_q, ff2_q, ff3_q, ff4_q : STD_LOGIC := '0'; 
begin

    -- Primeiro Flip-Flop JK (recebe o clock de CLK)
    process(CLK, PRESET, CLEAR)
    begin
        if (CLEAR = '0') then
            ff1_q <= '0';
        elsif (PRESET = '0') then
            ff1_q <= '1';
        elsif falling_edge(CLK) then
            if (T = '1') then
                ff1_q <= NOT ff1_q; 
            end if;
        end if;
    end process;

    -- Segundo Flip-Flop JK (recebe o clock de Q1)
    process(ff1_q, PRESET, CLEAR)
    begin
        if (CLEAR = '0') then
            ff2_q <= '0';
        elsif (PRESET = '0') then
            ff2_q <= '1';
        elsif falling_edge(ff1_q) then  -- O clock é o Q do FF1
           if (T = '1') then
                ff2_q <= NOT ff2_q; 
            end if;
        end if;
    end process;

    -- Terceiro Flip-Flop JK (recebe o clock de Q2)
    process(ff2_q, PRESET, CLEAR)
    begin
        if (CLEAR = '0') then
            ff3_q <= '0';
        elsif (PRESET = '0') then
            ff3_q <= '1';
        elsif falling_edge(ff2_q) then  -- O clock é o Q do FF2
          if (T = '1') then
                ff3_q <= NOT ff3_q; 
            end if;
        end if;
    end process;

    -- Quarto Flip-Flop JK (recebe o clock de Q3)
    process(ff3_q, PRESET, CLEAR)
    begin
        if (CLEAR = '0') then
            ff4_q <= '0';
        elsif (PRESET = '0') then
            ff4_q <= '1';
        elsif falling_edge(ff3_q) then  -- O clock é o Q do FF3
	       if (T = '1') then
	                ff4_q <= NOT ff4_q; 
            end if;
        end if;
    end process;

    -- Atribuição das saídas Q e QN
    Q1 <= ff1_q;
    Q1N <= NOT ff1_q;
    
    Q2 <= ff2_q;
    Q2N <= NOT ff2_q;

    Q3 <= ff3_q;
    Q3N <= NOT ff3_q;

    Q4 <= ff4_q;
    Q4N <= NOT ff4_q;

end Behavioral;

// VHDL entity jk_mestre_escravo_T, as the project stores it:
library IEEE;
use IEEE.STD_LOGIC_1164.ALL;

entity jk_mestre_escravo_T is
    Port (
        J      : in STD_LOGIC;            
        CLK    : in STD_LOGIC;        
        PRESET : in STD_LOGIC;        
        CLEAR  : in STD_LOGIC;       
        Q      : out STD_LOGIC;      
        QN     : out STD_LOGIC
    );
end jk_mestre_escravo_T;

architecture Behavioral of jk_mestre_escravo_T is
    signal master_q : STD_LOGIC := '0'; 
    signal slave_q : STD_LOGIC := '0';
begin

    process(CLK, PRESET, CLEAR)
    begin
        if (CLEAR = '0') then
            master_q <= '0';
        elsif (PRESET = '0') then
            master_q <= '1';
        elsif rising_edge(CLK) then
            if (J = '0') then
                master_q <= master_q; 
            elsif (J = '1') then
                master_q <= NOT master_q; 
            end if;
        end if;
    end process;

 
    process(CLK, PRESET, CLEAR)
    begin
        if (CLEAR = '0') then
            slave_q <= '0';
        elsif (PRESET = '0') then
            slave_q <= '1';
        elsif falling_edge(CLK) then
            slave_q <= master_q; 
        end if;
    end process;


    Q  <= slave_q;
    QN <= NOT slave_q;


end Behavioral;

// VHDL entity BiHex_VHDL, as the project stores it:
library IEEE;
use IEEE.STD_LOGIC_1164.ALL;

entity BiHex_VHDL is
    Port (
        A : in STD_LOGIC;
        B : in STD_LOGIC;
        C : in STD_LOGIC;
        D : in STD_LOGIC;
        aa   : out STD_LOGIC;
        bb  : out STD_LOGIC;
        cc   : out STD_LOGIC;
        dd   : out STD_LOGIC;
        e   : out STD_LOGIC;
        f   : out STD_LOGIC;
        g   : out STD_LOGIC
    );
end BiHex_VHDL;

architecture Behavioral of BiHex_VHDL is
begin
    aa <= (not B and not D) or (not A and C) or 
         (not A and B and D) or (A and not B and not C) or (A and not D) or 
         (B and C);

    bb <= (not A and not C and not D) or (not A and C and D) or 
         (not A and not B) or (not B and not D) or (A and not C and D);

    cc <= (not A and B) or (A and not B) or 
         (not C and D) or (not B and D) or (not B and not C);

    dd <= (B and not C and D) or (not A and not B and not D) or 
         (not B and C and D) or (A and not C) or 
         (B and C and not D);

    e <= (not B and not D) or (C and not D) or 
         (A and C) or (A and B);

    f <= (not C and not D) or (not A and B and not C) or 
         (B and not D) or (A and not B) or (A and C);

    g <= (not B and C) or (A and not B) or 
         (not A and B and not C) or (C and not D) or 
         (A and D);
end Behavioral;

// VHDL entity BinDisplay_VHDL, as the project stores it:
library IEEE;
use IEEE.STD_LOGIC_1164.ALL;

entity BinDisplay_VHDL is
    Port ( 
        A : in STD_LOGIC;
        aa   : out STD_LOGIC;
        b   : out STD_LOGIC;
        c   : out STD_LOGIC;
        d   : out STD_LOGIC;
        e   : out STD_LOGIC;
        f   : out STD_LOGIC;
        g   : out STD_LOGIC
    );
end BinDisplay_VHDL;

architecture Behavioral of BinDisplay_VHDL is
begin
    process(A)
    begin
  	  if A = '0' then
  	  	aa <= '1';
    		b <= '1';
    		c <= '1';
    		d <= '1';
    		e <= '1';
    		f <= '0';
    		g <= '1';
    	 else
    	 	aa <= '0';
    		b <= '1';
    		c <= '1';
    		d <= '0';
    		e <= '0';
    		f <= '0';
    		g <= '0';
    	  end if;
    end process;
end Behavioral;
