// Logisim project apresentacao.circ as structural Verilog
module main (
  input  [3:0] A,
  input  [3:0] B,
  input  in_3,
  output [4:0] out_4,
  output [3:0] out_5,
  output [4:0] out_6,
  output [3:0] out_7,
  output [4:0] out_8,
  output [4:0] out_9,
  output [4:0] out_10,
  output [4:0] out_11
);

  wire [3:0] complemento_vhdl_1_s;

  somador_4_bits somador_4_bits_1 (.in_1(A), .in_2(B), .out_3(out_4));
  somador_vhdl somador_vhdl_1 (.A(A), .B(B), .S(out_6));
  sumSub4bits sumsub4bits_1 (.A(A), .B(B), .M(in_3), .out_4(out_8));
  sumSubVHDL sumsubvhdl_1 (.A(A), .B(B), .M(in_3), .S(out_9));
  sub_4_bits sub_4_bits_1 (.in_1(A), .in_2(B), .out_3(out_5));
  subtrator_4_bits_vhdl subtrator_4_bits_vhdl_1 (.A(A), .B(B), .S(out_7));
  // Complemento complemento_1: pin names not known; wires that end beside it: B, A
  complemento_vhdl complemento_vhdl_1 (.B(B), .S(complemento_vhdl_1_s));
  somador_4_bits somador_4_bits_2 (.in_1(A), .out_3(out_10));  // open: in_2
  somador_4_bits somador_4_bits_3 (.in_1(A), .in_2(complemento_vhdl_1_s), .out_3(out_11));
endmodule

module meioSum (
  input  A,
  input  B,
  output S,
  output Carry
);

  xor xor_1 (S, A, B);
  and and_1 (Carry, A, B);
endmodule

module meio_sub (
  input  E,
  input  Cin,
  output S,
  output Cout
);

  wire not_1_out;

  not not_1 (not_1_out, E);
  xor xor_1 (S, E, Cin);
  and and_1 (Cout, Cin, not_1_out);
endmodule

module subComplemento1Bit (
  input  A,
  input  B,
  output out_3,
  output out_4
);

  wire not_1_out, xor_1_out;

  not not_1 (not_1_out, B);
  xor xor_1 (xor_1_out, 1'b1, not_1_out);
  xor xor_2 (out_3, A, xor_1_out);
  and and_1 (out_4, xor_1_out, A);
endmodule

module somadorCompleto (
  input  A,
  input  B,
  input  cin,
  output S,
  output cout
);

  wire meiosum_1_carry, meiosum_1_s, meiosum_2_carry;

  meioSum meiosum_1 (.A(A), .B(cin), .S(meiosum_1_s), .Carry(meiosum_1_carry));
  meioSum meiosum_2 (.A(meiosum_1_s), .B(B), .S(S), .Carry(meiosum_2_carry));
  or or_1 (cout, meiosum_2_carry, meiosum_1_carry);
endmodule

module somador_4_bits (
  input  [3:0] in_1,
  input  [3:0] in_2,
  output [4:0] out_3
);

  wire somadorcompleto_1_cout, somadorcompleto_2_cout, somadorcompleto_3_cout;

  somadorCompleto somadorcompleto_1 (.A(in_1[0]), .B(in_2[0]), .cin(1'b0), .S(out_3[0]), .cout(somadorcompleto_1_cout));
  somadorCompleto somadorcompleto_2 (
    .A(in_1[1]), .B(in_2[1]), .cin(somadorcompleto_1_cout), .S(out_3[1]), .cout(somadorcompleto_2_cout));
  somadorCompleto somadorcompleto_3 (
    .A(in_1[2]), .B(in_2[2]), .cin(somadorcompleto_2_cout), .S(out_3[2]), .cout(somadorcompleto_3_cout));
  somadorCompleto somadorcompleto_4 (
    .A(in_1[3]), .B(in_2[3]), .cin(somadorcompleto_3_cout), .S(out_3[3]), .cout(out_3[4]));
endmodule

module Complemento (
  input  [3:0] in_1,
  output [3:0] out_2
);

  wire not_1_out, not_2_out, not_3_out, not_4_out;

  not not_1 (not_1_out, in_1[0]);
  not not_2 (not_2_out, in_1[1]);
  not not_3 (not_3_out, in_1[2]);
  not not_4 (not_4_out, in_1[3]);
  fullSum4Bits fullsum4bits_1 (
    .A0(not_1_out), .A1(not_2_out), .A2(not_3_out), .A3(not_4_out), .B0(1'b1), .B1(1'b0), .B2(1'b0),
    .B3(1'b0), .S0(out_2[0]), .S1(out_2[1]), .S2(out_2[2]), .S3(out_2[3]));
endmodule

module fullSum (
  input  A,
  input  B,
  input  Cin,
  output S,
  output C
);

  wire meiosum_1_carry, meiosum_1_s, meiosum_2_carry;

  meioSum meiosum_1 (.A(A), .B(Cin), .S(meiosum_1_s), .Carry(meiosum_1_carry));
  meioSum meiosum_2 (.A(meiosum_1_s), .B(B), .S(S), .Carry(meiosum_2_carry));
  or or_1 (C, meiosum_1_carry, meiosum_2_carry);
endmodule

module fullSum4Bits (
  input  A0,
  input  A1,
  input  A2,
  input  A3,
  input  B0,
  input  B1,
  input  B2,
  input  B3,
  output S0,
  output S1,
  output S2,
  output S3
);

  wire fullsum_1_c, fullsum_2_c, fullsum_3_c;

  fullSum fullsum_1 (.A(A0), .B(B0), .Cin(1'b0), .S(S0), .C(fullsum_1_c));
  fullSum fullsum_2 (.A(A1), .B(B1), .Cin(fullsum_1_c), .S(S1), .C(fullsum_2_c));
  fullSum fullsum_3 (.A(A2), .B(B2), .Cin(fullsum_2_c), .S(S2), .C(fullsum_3_c));
  fullSum fullsum_4 (.A(A3), .B(B3), .Cin(fullsum_3_c), .S(S3));  // open: C
endmodule

module meioSubComplementos (
  input  in_1,
  input  in_2,
  input  in_3,
  output out_4,
  output out_5
);

  wire not_1_out, xor_1_out;

  xor xor_1 (xor_1_out, in_2, not_1_out);
  not not_1 (not_1_out, in_3);
  or or_1 (out_4, in_1, xor_1_out);
  and and_1 (out_5, in_1, xor_1_out);
endmodule

module sub_1_bit (
  input  A,
  input  B,
  input  cin,
  output S,
  output cout
);

  wire meio_sub_1_cout, meio_sub_1_s, meio_sub_2_cout;

  meio_sub meio_sub_1 (.E(A), .Cin(cin), .S(meio_sub_1_s), .Cout(meio_sub_1_cout));
  meio_sub meio_sub_2 (.E(meio_sub_1_s), .Cin(B), .S(S), .Cout(meio_sub_2_cout));
  or or_1 (cout, meio_sub_2_cout, meio_sub_1_cout);
endmodule

module sub_4_bits (
  input  [3:0] in_1,
  input  [3:0] in_2,
  output [3:0] out_3
);

  wire sub_1_bit_1_cout, sub_1_bit_2_cout, sub_1_bit_3_cout;

  sub_1_bit sub_1_bit_1 (.A(in_1[0]), .B(in_2[0]), .cin(1'b0), .S(out_3[0]), .cout(sub_1_bit_1_cout));
  sub_1_bit sub_1_bit_2 (.A(in_1[1]), .B(in_2[1]), .cin(sub_1_bit_1_cout), .S(out_3[1]), .cout(sub_1_bit_2_cout));
  sub_1_bit sub_1_bit_3 (.A(in_1[2]), .B(in_2[2]), .cin(sub_1_bit_2_cout), .S(out_3[2]), .cout(sub_1_bit_3_cout));
  sub_1_bit sub_1_bit_4 (.A(in_1[3]), .B(in_2[3]), .cin(sub_1_bit_3_cout), .S(out_3[3]));  // open: cout
endmodule

module meioSumSub (
  input  M,
  input  A,
  input  B,
  output out_4,
  output out_5
);

  wire xor_1_out;

  xor xor_1 (xor_1_out, A, M);
  xor xor_2 (out_4, A, B);
  and and_1 (out_5, B, xor_1_out);
endmodule

module sumSub4bits (
  input  [3:0] A,
  input  [3:0] B,
  input  M,
  output [4:0] out_4
);

  wire sumsubcompleto_1_carry, sumsubcompleto_2_carry, sumsubcompleto_3_carry;

  sumSubCompleto sumsubcompleto_1 (.M(M), .A(A[0]), .B(B[0]), .Cin(1'b0), .S(out_4[0]), .Carry(sumsubcompleto_1_carry));
  sumSubCompleto sumsubcompleto_2 (
    .M(M), .A(A[1]), .B(B[1]), .Cin(sumsubcompleto_1_carry), .S(out_4[1]), .Carry(sumsubcompleto_2_carry));
  sumSubCompleto sumsubcompleto_3 (
    .M(M), .A(A[2]), .B(B[2]), .Cin(sumsubcompleto_2_carry), .S(out_4[2]), .Carry(sumsubcompleto_3_carry));
  sumSubCompleto sumsubcompleto_4 (
    .M(M), .A(A[3]), .B(B[3]), .Cin(sumsubcompleto_3_carry), .S(out_4[3]), .Carry(out_4[4]));
endmodule

module sumSubCompleto (
  input  M,
  input  A,
  input  B,
  input  Cin,
  output S,
  output Carry
);

  wire meiosumsub_1_out_4, meiosumsub_1_out_5, meiosumsub_2_out_5;

  meioSumSub meiosumsub_1 (.M(M), .A(A), .B(Cin), .out_4(meiosumsub_1_out_4), .out_5(meiosumsub_1_out_5));
  meioSumSub meiosumsub_2 (.M(M), .A(meiosumsub_1_out_4), .B(B), .out_4(S), .out_5(meiosumsub_2_out_5));
  or or_1 (Carry, meiosumsub_1_out_5, meiosumsub_2_out_5);
endmodule

// VHDL entity somador_vhdl, as the project stores it:
LIBRARY ieee;
USE ieee.std_logic_1164.all;

ENTITY somador_vhdl IS
  PORT (
  ------------------------------------------------------------------------------
  --Insert input ports below
    A      : IN  std_logic_vector(3 DOWNTO 0);                   -- input bit example
    B       : IN  std_logic_vector(3 DOWNTO 0); -- input vector example
  ------------------------------------------------------------------------------
  --Insert output ports below
                  -- output bit example
    S        : OUT std_logic_vector(4 DOWNTO 0)
    
    );
END somador_vhdl;


--------------------------------------------------------------------------------
--Complete your VHDL description below
--------------------------------------------------------------------------------

ARCHITECTURE TypeArchitecture OF somador_vhdl IS
signal carry : std_logic_vector(3 DOWNTO 0);
BEGIN

S(0) <= A(0) xor B(0);
carry(1) <= A(0) and B(0);
S(1) <= ((A(1) xor carry(1)) xor B(1));
carry(2) <= (A(1) and carry(1)) or (B(1) and (A(1) xor carry(1)));
S(2) <= ((A(2) xor carry(2)) xor B(2));
carry(3) <= (A(2) and carry(2)) or (B(2) and (A(2) xor carry(2)));
S(3) <= ((A(3) xor carry(3)) xor B(3));
S(4) <= (A(3) and carry(3)) or (B(3) and (A(3) xor carry(3)));


END TypeArchitecture;

// VHDL entity complemento_vhdl, as the project stores it:
--------------------------------------------------------------------------------
-- Project :
-- File    :
-- Autor   :
-- Date    :
--
--------------------------------------------------------------------------------
-- Description :
-- Implementa o complemento de 2 de um vetor de entrada de 4 bits.
--------------------------------------------------------------------------------

LIBRARY ieee;
USE ieee.std_logic_1164.all;

ENTITY complemento_vhdl IS
  PORT (
    ----------------------------------------------------------------------------
    -- Insert input ports below
    B      : IN  std_logic_vector(3 DOWNTO 0); -- input vector example
    ----------------------------------------------------------------------------
    -- Insert output ports below
    S      : OUT std_logic_vector(3 DOWNTO 0)  -- Saída para o complemento de 2
  );
END complemento_vhdl;

ARCHITECTURE TypeArchitecture OF complemento_vhdl IS

  signal B_complemento : std_logic_vector(3 DOWNTO 0); -- Complemento de 1 de B
  signal carry         : std_logic_vector(3 DOWNTO 0); -- Sinal de carry

BEGIN

  -- Calcula o complemento de 1 de B
  B_complemento <= NOT B;

  -- Calcula o complemento de 2 ao adicionar 1 ao complemento de 1
  carry(0) <= '1'; -- Inicia com 1 para fazer complemento de 2
  S(0) <= B_complemento(0) XOR carry(0);
  carry(1) <= (B_complemento(0) AND carry(0));
  S(1) <= B_complemento(1) XOR carry(1);
  carry(2) <= (B_complemento(1) AND carry(1));
  S(2) <= B_complemento(2) XOR carry(2);
  carry(3) <= (B_complemento(2) AND carry(2));
  S(3) <= B_complemento(3) XOR carry(3);

END TypeArchitecture;

// VHDL entity subtrator_4_bits_vhdl, as the project stores it:
LIBRARY ieee;
USE ieee.std_logic_1164.all;

ENTITY subtrator_4_bits_vhdl IS
  PORT (
    A      : IN  std_logic_vector(3 DOWNTO 0); -- vetor de entrada A
    B      : IN  std_logic_vector(3 DOWNTO 0); -- vetor de entrada B
    S      : OUT std_logic_vector(3 DOWNTO 0)  -- vetor de saída S
  );
END subtrator_4_bits_vhdl;

ARCHITECTURE TypeArchitecture OF subtrator_4_bits_vhdl IS
  SIGNAL borrow : std_logic_vector(4 DOWNTO 0); -- vetores de borrow com bit extra para o último
BEGIN
  -- Inicializa o borrow inicial como '0'
  borrow(0) <= '0';

  gen_loop: for i in 0 to 3 generate
    S(i) <= A(i) xor B(i) xor borrow(i);
    borrow(i+1) <= ((not A(i)) and borrow(i)) or (((not A(i)) xnor ( not borrow(i))) and B(i)) ; 
  end generate;

END TypeArchitecture;

// VHDL entity sumSubVHDL, as the project stores it:
--------------------------------------------------------------------------------
-- Project :
-- File    :
-- Autor   :
-- Date    :
--
--------------------------------------------------------------------------------
-- Description :
--
--------------------------------------------------------------------------------

LIBRARY ieee;
USE ieee.std_logic_1164.all;

ENTITY sumSubVHDL IS
  PORT (
  ------------------------------------------------------------------------------
  --Insert input ports below
    A        : IN  std_logic_vector(3 DOWNTO 0);                    -- input bit example
    B        : IN  std_logic_vector(3 DOWNTO 0); -- input vector example
    M        : IN  std_logic;
    S        : OUT std_logic_vector(4 DOWNTO 0)  -- output vector example
    );
END sumSubVHDL;

--------------------------------------------------------------------------------
--Complete your VHDL description below
--------------------------------------------------------------------------------

ARCHITECTURE TypeArchitecture OF sumSubVHDL IS
signal C : std_logic_vector(3 DOWNTO 0);
BEGIN
	S(0) <= A(0) XOR B(0);
	C(1) <= B(0) AND (M XOR A(0));
	
	S(1) <= B(1) XOR (A(1) XOR C(1));
	C(2) <= (B(1) AND ((M XOR A(1)) XOR C(1))) OR ((M XOR A(1)) AND C(1));
	
	S(2) <= B(2) XOR (A(2) XOR C(2));
	C(3) <= (B(2) AND ((M XOR A(2)) XOR C(2))) OR ((M XOR A(2)) AND C(2));

	S(3) <= B(3) XOR (A(3) XOR C(3));
	S(4) <= (B(3) AND ((M XOR A(3)) XOR C(3))) OR ((M XOR A(3)) AND C(3));
	
END TypeArchitecture;

// VHDL entity subComplementoVHDL, as the project stores it:
LIBRARY ieee;
USE ieee.std_logic_1164.all;
USE ieee.numeric_std.all;  -- Para operações com unsigned

ENTITY subComplemento IS
  PORT (
    A      : IN  std_logic_vector(3 DOWNTO 0);  -- Vetor de entrada A
    B      : IN  std_logic_vector(3 DOWNTO 0);  -- Vetor de entrada B
    S      : OUT std_logic_vector(3 DOWNTO 0);  -- Saída (A - B)
    ov     : OUT std_logic                     -- Overflow
  );
END subComplemento;

ARCHITECTURE TypeArchitecture OF subComplemento IS
  signal B_complemento : std_logic_vector(3 DOWNTO 0);  -- Armazena o complemento de dois de B
  signal result        : unsigned(4 DOWNTO 0);         -- Resultado da soma com carry extra
BEGIN
  -- Inverter bit a bit B (primeira parte do complemento de dois)
  B_complemento &lt;= not B;

  -- Somar 1 a B_complemento (segunda parte do complemento de dois) e somar com A, ambos estendidos para 5 bits
  result &lt;= unsigned('0' &amp; A) + unsigned('0' &amp; B_complemento) + 1;

  -- Atribuir os 4 bits menos significativos do resultado à saída S
  S &lt;= std_logic_vector(result(3 DOWNTO 0));

  -- Detectar overflow (se o carry out do bit mais significativo for 1)
  ov &lt;= result(4);
  
END TypeArchitecture;
