// Logisim project somador_4_bits_com_vhdl.circ as structural Verilog
module main (
  input  [3:0] A,
  input  [3:0] B,
  output [4:0] out_3,
  output [4:0] out_4
);

  somador somador_1 (.A(A), .B(B), .S(out_3));
  somador_vhdl somador_vhdl_1 (.A(A), .B(B), .S(out_4));
endmodule

module meia_soma (
  input  Entrada,
  input  cin,
  output S,
  output cout
);

  and and_1 (cout, Entrada, cin);
  xor xor_1 (S, Entrada, cin);
endmodule

module somador (
  input  [3:0] A,
  input  [3:0] B,
  output [4:0] S
);

  somador_4_bits somador_4_bits_1 (
    .A3(A[3]), .A2(A[2]), .A1(A[1]), .A0(A[0]), .B3(B[3]), .B2(B[2]), .B1(B[1]), .B0(B[0]), .out_9(S[4]),
    .out_10(S[3]), .out_11(S[2]), .out_12(S[1]), .out_13(S[0]));
endmodule

module somador_completo (
  input  A,
  input  B,
  input  cin,
  output S,
  output carry
);

  wire meia_soma_1_cout, meia_soma_1_s, meia_soma_2_cout;

  meia_soma meia_soma_1 (.Entrada(A), .cin(cin), .S(meia_soma_1_s), .cout(meia_soma_1_cout));
  meia_soma meia_soma_2 (.Entrada(meia_soma_1_s), .cin(B), .S(S), .cout(meia_soma_2_cout));
  or or_1 (carry, meia_soma_2_cout, meia_soma_1_cout);
endmodule

module somador_4_bits (
  input  A3,
  input  A2,
  input  A1,
  input  A0,
  input  B3,
  input  B2,
  input  B1,
  input  B0,
  output out_9,
  output out_10,
  output out_11,
  output out_12,
  output out_13
);

  wire somador_completo_1_carry, somador_completo_2_carry, somador_completo_3_carry;

  somador_completo somador_completo_1 (.A(A0), .B(B0), .cin(1'b0), .S(out_13), .carry(somador_completo_1_carry));
  somador_completo somador_completo_2 (
    .A(A1), .B(B1), .cin(somador_completo_1_carry), .S(out_12), .carry(somador_completo_2_carry));
  somador_completo somador_completo_3 (
    .A(A2), .B(B2), .cin(somador_completo_2_carry), .S(out_11), .carry(somador_completo_3_carry));
  somador_completo somador_completo_4 (.A(A3), .B(B3), .cin(somador_completo_3_carry), .S(out_10), .carry(out_9));
endmodule

module somador_e_vhdl (
  input  A3,
  input  A2,
  input  A1,
  input  A0,
  input  B3,
  input  B2,
  input  B1,
  input  B0,
  output out_9,
  output out_10,
  output out_11,
  output out_12,
  output S0,
  output [3:0] out_14,
  output out_15
);

  somador_4_bits somador_4_bits_1 (
    .A3(A3), .A2(A2), .A1(A1), .A0(A0), .B3(B3), .B2(B2), .B1(B1), .B0(B0), .out_9(out_9), .out_10(out_10),
    .out_11(out_11), .out_12(out_12), .out_13(S0));
  // somador_vhdl somador_vhdl_1: pin names not known; wires that end beside it: {A3, A2, A1, A0}, {B3, B2, B1, B0}, out_14, out_15
endmodule

// VHDL entity somador_vhdl, as the project stores it:
LIBRARY ieee;
USE ieee.std_logic_1164.all;

ENTITY somador_vhdl IS
  PORT (
  ------------------------------------------------------------------------------
  --Insert input ports below
    A      : IN  std_logic_vector(3 DOWNTO 0);                   -- input bit example
    B       : IN  std_logic_vector(3 DOWNTO 0); -- input vector example
  ------------------------------------------------------------------------------
  --Insert output ports below
                  -- output bit example
    S        : OUT std_logic_vector(4 DOWNTO 0)
    
    );
END somador_vhdl;


--------------------------------------------------------------------------------
--Complete your VHDL description below
--------------------------------------------------------------------------------

ARCHITECTURE TypeArchitecture OF somador_vhdl IS
signal carry : std_logic_vector(3 DOWNTO 0);
BEGIN

S(0) <= A(0) xor B(0);
carry(1) <= A(0) and B(0);
S(1) <= ((A(1) xor carry(1)) xor B(1));
carry(2) <= (A(1) and carry(1)) or (B(1) and (A(1) xor carry(1)));
S(2) <= ((A(2) xor carry(2)) xor B(2));
carry(3) <= (A(2) and carry(2)) or (B(2) and (A(2) xor carry(2)));
S(3) <= ((A(3) xor carry(3)) xor B(3));
S(4) <= (A(3) and carry(3)) or (B(3) and (A(3) xor carry(3)));


END TypeArchitecture;
