// Logisim project subComplemento.circ as structural Verilog
module main (
  input  A0,
  input  A1,
  input  A2,
  input  A3,
  input  B0,
  input  B1,
  input  B2,
  input  B3,
  output S0,
  output S1,
  output S2,
  output S3,
  output [3:0] out_13
);

  wire complemento_1_out_5, complemento_1_out_6, complemento_1_out_7, complemento_1_out_8;
  wire [3:0] complemento_vhdl_1_s;

  Complemento complemento_1 (
    .in_1(B0), .in_2(B1), .in_3(B2), .in_4(B3), .out_5(complemento_1_out_5), .out_6(complemento_1_out_6),
    .out_7(complemento_1_out_7), .out_8(complemento_1_out_8));
  complemento_vhdl complemento_vhdl_1 (.B({B3, B2, B1, B0}), .S(complemento_vhdl_1_s));
  fullSum4Bits fullsum4bits_1 (
    .A0(A0), .A1(A1), .A2(A2), .A3(A3), .B0(complemento_1_out_5), .B1(complemento_1_out_6),
    .B2(complemento_1_out_7), .B3(complemento_1_out_8), .S0(S0), .S1(S1), .S2(S2), .S3(S3));
  somador_vhdl somador_vhdl_1 (.A({A3, A2, A1, A0}), .B(complemento_vhdl_1_s), .S(out_13));
endmodule

module meioSum (
  input  A,
  input  B,
  output S,
  output Carry
);

  xor xor_1 (S, A, B);
  and and_1 (Carry, A, B);
endmodule

module Complemento (
  input  in_1,
  input  in_2,
  input  in_3,
  input  in_4,
  output out_5,
  output out_6,
  output out_7,
  output out_8
);

  wire not_1_out, not_2_out, not_3_out, not_4_out;

  not not_1 (not_1_out, in_1);
  not not_2 (not_2_out, in_2);
  not not_3 (not_3_out, in_3);
  not not_4 (not_4_out, in_4);
  fullSum4Bits fullsum4bits_1 (
    .A0(not_1_out), .A1(not_2_out), .A2(not_3_out), .A3(not_4_out), .B0(1'b1), .B1(1'b0), .B2(1'b0),
    .B3(1'b0), .S0(out_5), .S1(out_6), .S2(out_7), .S3(out_8));
endmodule

module fullSum (
  input  A,
  input  B,
  input  Cin,
  output S,
  output C
);

  wire meiosum_1_carry, meiosum_1_s, meiosum_2_carry;

  meioSum meiosum_1 (.A(A), .B(Cin), .S(meiosum_1_s), .Carry(meiosum_1_carry));
  meioSum meiosum_2 (.A(meiosum_1_s), .B(B), .S(S), .Carry(meiosum_2_carry));
  or or_1 (C, meiosum_1_carry, meiosum_2_carry);
endmodule

module fullSum4Bits (
  input  A0,
  input  A1,
  input  A2,
  input  A3,
  input  B0,
  input  B1,
  input  B2,
  input  B3,
  output S0,
  output S1,
  output S2,
  output S3
);

  wire fullsum_1_c, fullsum_2_c, fullsum_3_c;

  fullSum fullsum_1 (.A(A0), .B(B0), .Cin(1'b0), .S(S0), .C(fullsum_1_c));
  fullSum fullsum_2 (.A(A1), .B(B1), .Cin(fullsum_1_c), .S(S1), .C(fullsum_2_c));
  fullSum fullsum_3 (.A(A2), .B(B2), .Cin(fullsum_2_c), .S(S2), .C(fullsum_3_c));
  fullSum fullsum_4 (.A(A3), .B(B3), .Cin(fullsum_3_c), .S(S3));  // open: C
endmodule

module meioSubComplementos (
  input  in_1,
  input  in_2,
  input  in_3,
  output out_4,
  output out_5
);

  wire not_1_out, xor_1_out;

  xor xor_1 (xor_1_out, in_2, not_1_out);
  not not_1 (not_1_out, in_3);
  or or_1 (out_4, in_1, xor_1_out);
  and and_1 (out_5, in_1, xor_1_out);
endmodule

// VHDL entity subComplemento, as the project stores it:
LIBRARY ieee;
USE ieee.std_logic_1164.all;
USE ieee.numeric_std.all;  -- Para operações com unsigned

ENTITY subComplemento IS
  PORT (
    A      : IN  std_logic_vector(3 DOWNTO 0);  -- Vetor de entrada A
    B      : IN  std_logic_vector(3 DOWNTO 0);  -- Vetor de entrada B
    S      : OUT std_logic_vector(3 DOWNTO 0);  -- Saída (A - B)
    ov : OUT std_logic
  );
END subComplemento;

ARCHITECTURE TypeArchitecture OF subComplemento IS
  signal B_complemento : std_logic_vector(3 DOWNTO 0);  -- Armazena o complemento de dois de B
  signal result        : unsigned(4 DOWNTO 0);         -- Resultado da soma com carry extra
BEGIN
  -- Inverter bit a bit B (primeira parte do complemento de dois)
  B_complemento <= not B;

  -- Somar 1 a B_complemento (segunda parte do complemento de dois) e somar com A, ambos estendidos para 5 bits
  result <= unsigned('0' & A) + unsigned('0' & B_complemento) + 1;

  -- Atribuir os 4 bits menos significativos do resultado à saída S
  S <= std_logic_vector(result(3 DOWNTO 0));
  ov <= result(4);  -- Detectar overflow (se o carry out do bit mais significativo for 1)
END TypeArchitecture;

// VHDL entity complemento_vhdl, as the project stores it:
--------------------------------------------------------------------------------
-- Project :
-- File    :
-- Autor   :
-- Date    :
--
--------------------------------------------------------------------------------
-- Description :
-- Implementa o complemento de 2 de um vetor de entrada de 4 bits.
--------------------------------------------------------------------------------

LIBRARY ieee;
USE ieee.std_logic_1164.all;

ENTITY complemento_vhdl IS
  PORT (
    ----------------------------------------------------------------------------
    -- Insert input ports below
    B      : IN  std_logic_vector(3 DOWNTO 0); -- input vector example
    ----------------------------------------------------------------------------
    -- Insert output ports below
    S      : OUT std_logic_vector(3 DOWNTO 0)  -- Saída para o complemento de 2
  );
END complemento_vhdl;

ARCHITECTURE TypeArchitecture OF complemento_vhdl IS

  signal B_complemento : std_logic_vector(3 DOWNTO 0); -- Complemento de 1 de B
  signal carry         : std_logic_vector(3 DOWNTO 0); -- Sinal de carry

BEGIN

  -- Calcula o complemento de 1 de B
  B_complemento <= NOT B;

  -- Calcula o complemento de 2 ao adicionar 1 ao complemento de 1
  carry(0) <= '1'; -- Inicia com 1 para fazer complemento de 2
  S(0) <= B_complemento(0) XOR carry(0);
  carry(1) <= (B_complemento(0) AND carry(0));
  S(1) <= B_complemento(1) XOR carry(1);
  carry(2) <= (B_complemento(1) AND carry(1));
  S(2) <= B_complemento(2) XOR carry(2);
  carry(3) <= (B_complemento(2) AND carry(2));
  S(3) <= B_complemento(3) XOR carry(3);

END TypeArchitecture;

// VHDL entity somador_vhdl, as the project stores it:
LIBRARY ieee;
USE ieee.std_logic_1164.all;

ENTITY somador_vhdl IS
  PORT (
  ------------------------------------------------------------------------------
  --Insert input ports below
    A      : IN  std_logic_vector(3 DOWNTO 0);                   -- input bit example
    B       : IN  std_logic_vector(3 DOWNTO 0); -- input vector example
  ------------------------------------------------------------------------------
  --Insert output ports below
                  -- output bit example
    S        : OUT std_logic_vector(3 DOWNTO 0)
    
    );
END somador_vhdl;


--------------------------------------------------------------------------------
--Complete your VHDL description below
--------------------------------------------------------------------------------

ARCHITECTURE TypeArchitecture OF somador_vhdl IS
signal carry : std_logic_vector(3 DOWNTO 0);
BEGIN

S(0) <= A(0) xor B(0);
carry(1) <= A(0) and B(0);
S(1) <= ((A(1) xor carry(1)) xor B(1));
carry(2) <= (A(1) and carry(1)) or (B(1) and (A(1) xor carry(1)));
S(2) <= ((A(2) xor carry(2)) xor B(2));
carry(3) <= (A(2) and carry(2)) or (B(2) and (A(2) xor carry(2)));
S(3) <= ((A(3) xor carry(3)) xor B(3));



END TypeArchitecture;
