// Logisim project subtrator_4_bits_com_vhdl.circ as structural Verilog
module meio_sub (
  input  E,
  input  Cin,
  output S,
  output Cout
);

  wire not_1_out;

  not not_1 (not_1_out, E);
  xor xor_1 (S, E, Cin);
  and and_1 (Cout, Cin, not_1_out);
endmodule

module sub_1_bit (
  input  A,
  input  B,
  input  cin,
  output S,
  output cout
);

  wire meio_sub_1_cout, meio_sub_1_s, meio_sub_2_cout;

  meio_sub meio_sub_1 (.E(A), .Cin(cin), .S(meio_sub_1_s), .Cout(meio_sub_1_cout));
  meio_sub meio_sub_2 (.E(meio_sub_1_s), .Cin(B), .S(S), .Cout(meio_sub_2_cout));
  or or_1 (cout, meio_sub_2_cout, meio_sub_1_cout);
endmodule

module sub_4_bits (
  input  A3,
  input  A2,
  input  A1,
  input  A0,
  input  B3,
  input  B2,
  input  B1,
  input  B0,
  output S3,
  output S2,
  output S1,
  output S0
);

  wire sub_1_bit_1_cout, sub_1_bit_2_cout, sub_1_bit_3_cout;

  sub_1_bit sub_1_bit_1 (.A(A0), .B(B0), .cin(1'b0), .S(S0), .cout(sub_1_bit_1_cout));
  sub_1_bit sub_1_bit_2 (.A(A1), .B(B1), .cin(sub_1_bit_1_cout), .S(S1), .cout(sub_1_bit_2_cout));
  sub_1_bit sub_1_bit_3 (.A(A2), .B(B2), .cin(sub_1_bit_2_cout), .S(S2), .cout(sub_1_bit_3_cout));
  sub_1_bit sub_1_bit_4 (.A(A3), .B(B3), .cin(sub_1_bit_3_cout), .S(S3));  // open: cout
endmodule

module sub_com_vhl_e_sem (
  input  A3,
  input  A2,
  input  A1,
  input  A0,
  input  B3,
  input  B2,
  input  B1,
  input  B0,
  output out_9,
  output out_10,
  output out_11,
  output out_12,
  output [3:0] out_13
);

  sub_4_bits sub_4_bits_1 (
    .A3(A3), .A2(A2), .A1(A1), .A0(A0), .B3(B3), .B2(B2), .B1(B1), .B0(B0), .S3(out_9), .S2(out_10),
    .S1(out_11), .S0(out_12));
  subtrator_4_bits_vhdl subtrator_4_bits_vhdl_1 (.A({A3, A2, A1, A0}), .B({B3, B2, B1, B0}), .S(out_13));
endmodule

// VHDL entity subtrator_4_bits_vhdl, as the project stores it:
LIBRARY ieee;
USE ieee.std_logic_1164.all;

ENTITY subtrator_4_bits_vhdl IS
  PORT (
    A      : IN  std_logic_vector(3 DOWNTO 0); -- vetor de entrada A
    B      : IN  std_logic_vector(3 DOWNTO 0); -- vetor de entrada B
    S      : OUT std_logic_vector(3 DOWNTO 0)  -- vetor de saída S
  );
END subtrator_4_bits_vhdl;

ARCHITECTURE TypeArchitecture OF subtrator_4_bits_vhdl IS
  SIGNAL borrow : std_logic_vector(4 DOWNTO 0); -- vetores de borrow com bit extra para o último
BEGIN
  -- Inicializa o borrow inicial como '0'
  borrow(0) <= '0';

  gen_loop: for i in 0 to 3 generate
    S(i) <= A(i) xor B(i) xor borrow(i);
    borrow(i+1) <= ((not A(i)) and borrow(i)) or (((not A(i)) xnor ( not borrow(i))) and B(i)) ; 
  end generate;

END TypeArchitecture;
