// Logisim project Mux.circ as structural Verilog
module main (
  input  [3:0] A,
  input  [3:0] B,
  input  in_3,
  input  [2:0] Sel,
  output [4:0] out_5,
  output [4:0] out_6
);

  TrabalhoFinal1 trabalhofinal1_1 (.A(A), .B(B), .Enable(in_3), .in_4(Sel), .out_5(out_5));
  trabalhoFinal1VHDL trabalhofinal1vhdl_1 (.A(A), .B(B), .Enabler(in_3), .Sel(Sel), .out_5(out_6));
endmodule

module MUX (
  input  Entrada1,
  input  Entrada2,
  input  in_3,
  output out_4
);

  wire and_1_out, and_2_out;

  and and_1 (and_1_out, Entrada1, ~in_3);  // AND_Gate
  and and_2 (and_2_out, Entrada2, in_3);
  or or_1 (out_4, and_1_out, and_2_out);
endmodule

module MUX2 (
  input  A,
  input  B,
  input  C,
  input  D,
  input  SEL1,
  input  SEL2,
  output S
);

  wire mux_1_out_4, mux_2_out_4;

  MUX mux_1 (.Entrada1(A), .Entrada2(B), .in_3(SEL1), .out_4(mux_1_out_4));
  MUX mux_2 (.Entrada1(C), .Entrada2(D), .in_3(SEL1), .out_4(mux_2_out_4));
  MUX mux_3 (.Entrada1(mux_1_out_4), .Entrada2(mux_2_out_4), .in_3(SEL2), .out_4(S));
endmodule

module MUX3 (
  input  A,
  input  B,
  input  C,
  input  D,
  input  E,
  input  F,
  input  G,
  input  H,
  input  SEL2,
  input  SEL1,
  input  SEL3,
  output out_12
);

  wire mux2_1_s, mux2_2_s;

  MUX2 mux2_1 (.A(A), .B(B), .C(C), .D(D), .SEL1(SEL1), .SEL2(SEL2), .S(mux2_1_s));
  MUX2 mux2_2 (.A(E), .B(F), .C(G), .D(H), .SEL1(SEL1), .SEL2(SEL2), .S(mux2_2_s));
  MUX mux_1 (.Entrada1(mux2_1_s), .Entrada2(mux2_2_s), .in_3(SEL3), .out_4(out_12));
endmodule

module Demux (
  input  A,
  input  Sel,
  output out_3,
  output out_4
);

  and and_1 (out_3, ~Sel, A);  // AND_Gate
  and and_2 (out_4, A, Sel);
endmodule

module Demux2 (
  input  A,
  input  Sel1,
  input  Sel2,
  output A0,
  output B0,
  output A2,
  output B2
);

  wire demux_1_out_3, demux_1_out_4;

  Demux demux_1 (.A(A), .Sel(Sel2), .out_3(demux_1_out_3), .out_4(demux_1_out_4));
  Demux demux_2 (.A(demux_1_out_3), .Sel(Sel1), .out_3(A0), .out_4(B0));
  Demux demux_3 (.A(demux_1_out_4), .Sel(Sel1), .out_3(A2), .out_4(B2));
endmodule

module Demux3 (
  input  A,
  input  Sel3,
  input  Sel2,
  input  Sel1,
  output S0,
  output S1,
  output S2,
  output S3,
  output S4,
  output S5,
  output S6,
  output S7
);

  wire demux2_1_a0, demux2_1_b2;

  Demux2 demux2_1 (.A(A), .Sel1(Sel3), .Sel2(Sel3), .A0(demux2_1_a0), .B2(demux2_1_b2));  // open: B0, A2
  Demux2 demux2_2 (.A(demux2_1_a0), .Sel1(Sel1), .Sel2(Sel2), .A0(S0), .B0(S1), .A2(S2), .B2(S3));
  Demux2 demux2_3 (.A(demux2_1_b2), .Sel1(Sel1), .Sel2(Sel2), .A0(S4), .B0(S5), .A2(S6), .B2(S7));
endmodule

module DetectorDeZero (
  input  A3,
  input  A2,
  input  A1,
  input  A0,
  input  enabler,
  output S
);

  wire not_1_out, or_1_out;

  or or_1 (or_1_out, A3, A2, A1, A0);
  not not_1 (not_1_out, or_1_out);
  and and_1 (S, not_1_out, enabler);
endmodule

module meiaSoma (
  input  A,
  input  B,
  input  cin,
  output S,
  output cout
);

  wire and_1_out, and_2_out, xor_1_out;

  xor xor_1 (xor_1_out, A, cin);
  and and_1 (and_1_out, A, cin);
  xor xor_2 (S, xor_1_out, B);
  and and_2 (and_2_out, xor_1_out, B);
  or or_1 (cout, and_2_out, and_1_out);
endmodule

module somador_4_bits (
  input  A3,
  input  A2,
  input  A1,
  input  A0,
  input  B3,
  input  B2,
  input  B1,
  input  B0,
  input  ENABLER,
  output S4,
  output S3,
  output S2,
  output S1,
  output S0
);

  wire and_1_out, and_2_out, and_3_out, and_4_out, and_5_out, and_6_out, and_7_out, and_8_out,
       meiasoma_1_cout, meiasoma_2_cout, meiasoma_3_cout;

  and and_1 (and_1_out, A3, ENABLER);
  and and_2 (and_2_out, A2, ENABLER);
  and and_3 (and_3_out, A1, ENABLER);
  and and_4 (and_4_out, A0, ENABLER);
  and and_5 (and_5_out, B3, ENABLER);
  and and_6 (and_6_out, B2, ENABLER);
  and and_7 (and_7_out, B1, ENABLER);
  and and_8 (and_8_out, B0, ENABLER);
  meiaSoma meiasoma_1 (.A(and_4_out), .B(and_8_out), .cin(1'b0), .S(S0), .cout(meiasoma_1_cout));
  meiaSoma meiasoma_2 (.A(and_3_out), .B(and_7_out), .cin(meiasoma_1_cout), .S(S1), .cout(meiasoma_2_cout));
  meiaSoma meiasoma_3 (.A(and_2_out), .B(and_6_out), .cin(meiasoma_2_cout), .S(S2), .cout(meiasoma_3_cout));
  meiaSoma meiasoma_4 (.A(and_1_out), .B(and_5_out), .cin(meiasoma_3_cout), .S(S3), .cout(S4));
endmodule

module somador_e_vhdl (
  input  A3,
  input  A2,
  input  A1,
  input  A0,
  input  B3,
  input  B2,
  input  B1,
  input  B0,
  output out_9,
  output out_10,
  output out_11,
  output out_12,
  output ov,
  output [3:0] out_14,
  output out_15
);

  somador_4_bits somador_4_bits_1 (
    .A3(A3), .A2(A2), .A1(A1), .A0(A0), .B3(B3), .B2(B2), .B1(B1), .B0(B0), .S4(out_9), .S3(out_10),
    .S2(out_11), .S1(out_12), .S0(ov));  // open: ENABLER
endmodule

module meio_sub (
  input  E,
  input  Cin,
  output S,
  output Cout
);

  wire not_1_out;

  not not_1 (not_1_out, E);
  xor xor_1 (S, E, Cin);
  and and_1 (Cout, Cin, not_1_out);
endmodule

module sub_1_bit (
  input  A,
  input  B,
  input  cin,
  output S,
  output cout
);

  wire meio_sub_1_cout, meio_sub_1_s, meio_sub_2_cout;

  meio_sub meio_sub_1 (.E(A), .Cin(cin), .S(meio_sub_1_s), .Cout(meio_sub_1_cout));
  meio_sub meio_sub_2 (.E(meio_sub_1_s), .Cin(B), .S(S), .Cout(meio_sub_2_cout));
  or or_1 (cout, meio_sub_2_cout, meio_sub_1_cout);
endmodule

module sub_4_bits (
  input  A3,
  input  A2,
  input  A1,
  input  A0,
  input  B3,
  input  B2,
  input  B1,
  input  B0,
  output S3,
  output S2,
  output S1,
  output S0
);

  wire sub_1_bit_1_cout, sub_1_bit_2_cout, sub_1_bit_3_cout;

  sub_1_bit sub_1_bit_1 (.A(A0), .B(B0), .cin(1'b0), .S(S0), .cout(sub_1_bit_1_cout));
  sub_1_bit sub_1_bit_2 (.A(A1), .B(B1), .cin(sub_1_bit_1_cout), .S(S1), .cout(sub_1_bit_2_cout));
  sub_1_bit sub_1_bit_3 (.A(A2), .B(B2), .cin(sub_1_bit_2_cout), .S(S2), .cout(sub_1_bit_3_cout));
  sub_1_bit sub_1_bit_4 (.A(A3), .B(B3), .cin(sub_1_bit_3_cout), .S(S3));  // open: cout
endmodule

module sub_com_vhl_e_sem (
  input  A3,
  input  A2,
  input  A1,
  input  A0,
  input  B3,
  input  B2,
  input  B1,
  input  B0,
  input  Enabler,
  output S3,
  output S2,
  output S1,
  output S0
);

  wire and_1_out, and_2_out, and_3_out, and_4_out, and_5_out, and_6_out, and_7_out, and_8_out;

  and and_1 (and_1_out, A3, Enabler);
  and and_2 (and_2_out, A2, Enabler);
  and and_3 (and_3_out, A1, Enabler);
  and and_4 (and_4_out, B3, Enabler);
  and and_5 (and_5_out, B2, Enabler);
  and and_6 (and_6_out, B1, Enabler);
  and and_7 (and_7_out, B0, Enabler);
  and and_8 (and_8_out, A0, Enabler);
  sub_4_bits sub_4_bits_1 (
    .A3(and_1_out), .A2(and_2_out), .A1(and_3_out), .A0(and_8_out), .B3(and_4_out), .B2(and_5_out),
    .B1(and_6_out), .B0(and_7_out), .S3(S3), .S2(S2), .S1(S1), .S0(S0));
endmodule

module meioSum (
  input  A,
  input  B,
  output S,
  output Carry
);

  xor xor_1 (S, A, B);
  and and_1 (Carry, A, B);
endmodule

module Complemento (
  input  B0,
  input  B1,
  input  B2,
  input  B3,
  output S3,
  output S2,
  output S1,
  output S0
);

  wire not_1_out, not_2_out, not_3_out, not_4_out;

  not not_1 (not_1_out, B0);
  not not_2 (not_2_out, B1);
  not not_3 (not_3_out, B2);
  not not_4 (not_4_out, B3);
  fullSum4Bits fullsum4bits_1 (
    .A0(not_1_out), .A1(not_2_out), .A2(not_3_out), .A3(not_4_out), .B3(1'b0), .B2(1'b0), .B1(1'b0),
    .B0(1'b1), .S3(S3), .S2(S2), .S1(S1), .S0(S0));
endmodule

module fullSum (
  input  A,
  input  B,
  input  Cin,
  output S,
  output C
);

  wire meiosum_1_carry, meiosum_1_s, meiosum_2_carry;

  meioSum meiosum_1 (.A(A), .B(Cin), .S(meiosum_1_s), .Carry(meiosum_1_carry));
  meioSum meiosum_2 (.A(meiosum_1_s), .B(B), .S(S), .Carry(meiosum_2_carry));
  or or_1 (C, meiosum_1_carry, meiosum_2_carry);
endmodule

module fullSum4Bits (
  input  A0,
  input  A1,
  input  A2,
  input  A3,
  input  B3,
  input  B2,
  input  B1,
  input  B0,
  output S3,
  output S2,
  output S1,
  output S0
);

  wire fullsum_1_c, fullsum_2_c, fullsum_3_c;

  fullSum fullsum_1 (.A(A0), .B(B0), .Cin(1'b0), .S(S0), .C(fullsum_1_c));
  fullSum fullsum_2 (.A(A1), .B(B1), .Cin(fullsum_1_c), .S(S1), .C(fullsum_2_c));
  fullSum fullsum_3 (.A(A2), .B(B2), .Cin(fullsum_2_c), .S(S2), .C(fullsum_3_c));
  fullSum fullsum_4 (.A(A3), .B(B3), .Cin(fullsum_3_c), .S(S3));  // open: C
endmodule

module meioSubComplementos (
  input  in_1,
  input  in_2,
  input  in_3,
  output out_4,
  output out_5
);

  wire not_1_out, xor_1_out;

  xor xor_1 (xor_1_out, in_2, not_1_out);
  not not_1 (not_1_out, in_3);
  or or_1 (out_4, in_1, xor_1_out);
  and and_1 (out_5, in_1, xor_1_out);
endmodule

module SubComplemento (
  input  A3,
  input  A2,
  input  A1,
  input  A0,
  input  B3,
  input  B2,
  input  B1,
  input  B0,
  input  Enabler,
  output S3,
  output S2,
  output S1,
  output S0
);

  wire and_1_out, and_2_out, and_3_out, and_4_out, and_5_out, and_6_out, and_7_out, and_8_out,
       complemento_1_s0, complemento_1_s1, complemento_1_s2, complemento_1_s3;

  and and_1 (and_1_out, A0, Enabler);
  and and_2 (and_2_out, A1, Enabler);
  and and_3 (and_3_out, A2, Enabler);
  and and_4 (and_4_out, A3, Enabler);
  Complemento complemento_1 (
    .B0(B0), .B1(B1), .B2(B2), .B3(B3), .S3(complemento_1_s3), .S2(complemento_1_s2), .S1(complemento_1_s1),
    .S0(complemento_1_s0));
  and and_5 (and_5_out, complemento_1_s3, Enabler);
  and and_6 (and_6_out, complemento_1_s2, Enabler);
  and and_7 (and_7_out, complemento_1_s1, Enabler);
  and and_8 (and_8_out, complemento_1_s0, Enabler);
  fullSum4Bits fullsum4bits_1 (
    .A0(and_1_out), .A1(and_2_out), .A2(and_3_out), .A3(and_4_out), .B3(and_5_out), .B2(and_6_out),
    .B1(and_7_out), .B0(and_8_out), .S3(S3), .S2(S2), .S1(S1), .S0(S0));
endmodule

module andy (
  input  A3,
  input  A2,
  input  A1,
  input  A0,
  input  B3,
  input  B2,
  input  B1,
  input  B0,
  input  ENABLER,
  output S3,
  output S2,
  output S1,
  output S0
);

  wire and_1_out, and_2_out, and_3_out, and_4_out, and_5_out, and_6_out, and_7_out, and_8_out;

  and and_1 (and_1_out, A0, ENABLER);
  and and_2 (and_2_out, A1, ENABLER);
  and and_3 (and_3_out, A2, ENABLER);
  and and_4 (and_4_out, A3, ENABLER);
  and and_5 (and_5_out, B0, ENABLER);
  and and_6 (and_6_out, B1, ENABLER);
  and and_7 (and_7_out, B2, ENABLER);
  and and_8 (and_8_out, B3, ENABLER);
  and and_9 (S1, and_2_out, and_6_out);
  and and_10 (S2, and_3_out, and_7_out);
  and and_11 (S3, and_4_out, and_8_out);
  and and_12 (S0, and_1_out, and_5_out);
endmodule

module OR2 (
  input  A3,
  input  A2,
  input  A1,
  input  A0,
  input  B3,
  input  B2,
  input  B1,
  input  B0,
  input  in_9,
  output S3,
  output S2,
  output S1,
  output S0
);

  wire and_1_out, and_2_out, and_3_out, and_4_out, and_5_out, and_6_out, and_7_out, and_8_out;

  and and_1 (and_1_out, A3, in_9);
  and and_2 (and_2_out, A2, in_9);
  and and_3 (and_3_out, A1, in_9);
  and and_4 (and_4_out, A0, in_9);
  and and_5 (and_5_out, B3, in_9);
  and and_6 (and_6_out, B2, in_9);
  and and_7 (and_7_out, B1, in_9);
  and and_8 (and_8_out, B0, in_9);
  or or_1 (S3, and_1_out, and_5_out);
  or or_2 (S2, and_2_out, and_6_out);
  or or_3 (S1, and_3_out, and_7_out);
  or or_4 (S0, and_4_out, and_8_out);
endmodule

module seletor (
  input  nada,
  input  esquerda,
  input  Direita,
  input  [1:0] B,
  output S
);

  wire and_1_out, and_2_out, and_3_out, not_1_out, not_2_out, not_3_out, not_4_out;

  not not_1 (not_1_out, B[0]);
  not not_2 (not_2_out, B[1]);
  not not_3 (not_3_out, B[0]);
  not not_4 (not_4_out, B[1]);
  and and_1 (and_1_out, not_1_out, nada, not_2_out);
  and and_2 (and_2_out, not_3_out, esquerda, B[1]);
  and and_3 (and_3_out, B[0], Direita, not_4_out);
  or or_1 (S, and_1_out, and_2_out, and_3_out);
endmodule

module deslocamento (
  input  [3:0] in_1,
  input  [1:0] in_2,
  input  in_3,
  output [3:0] out_4,
  output [3:0] out_5
);

  wire [3:2] undriven;

  deslocador deslocador_1 (
    .A3(in_1[3]), .A2(in_1[2]), .A1(in_1[1]), .A0(in_1[0]), .B1(in_2[1]), .B0(in_2[0]), .Enabler(in_3),
    .S3(out_4[3]), .S2(out_4[2]), .S1(out_4[1]), .S0(out_4[0]));
  DeslocadorVHDL deslocadorvhdl_1 (.A(in_1), .B({undriven, in_2}), .C(in_3), .S(out_5));
  // Pins of 2 and 4 bits meet at {undriven, in_2}
endmodule

module seletor_cicuito (
  input  soma,
  input  B,
  input  Deslocar,
  output out_4
);

  wire and_1_out, and_2_out, not_1_out;

  not not_1 (not_1_out, B);
  and and_1 (and_1_out, soma, not_1_out);
  and and_2 (and_2_out, Deslocar, B);
  or or_1 (out_4, and_1_out, and_2_out);
endmodule

module deslocador (
  input  A3,
  input  A2,
  input  A1,
  input  A0,
  input  B1,
  input  B0,
  input  Enabler,
  output S3,
  output S2,
  output S1,
  output S0
);

  wire and_1_out, and_2_out, and_3_out, and_4_out;

  and and_1 (and_1_out, Enabler, A3);
  and and_2 (and_2_out, Enabler, A2);
  and and_3 (and_3_out, Enabler, A1);
  seletor seletor_1 (.nada(and_1_out), .esquerda(and_2_out), .Direita(1'b0), .B({B1, B0}), .S(S3));
  and and_4 (and_4_out, Enabler, A0);
  seletor seletor_2 (.nada(and_2_out), .esquerda(and_3_out), .Direita(and_1_out), .B({B1, B0}), .S(S2));
  seletor seletor_3 (.nada(and_3_out), .esquerda(and_4_out), .Direita(and_2_out), .B({B1, B0}), .S(S1));
  seletor seletor_4 (.nada(and_4_out), .esquerda(1'b0), .Direita(and_3_out), .B({B1, B0}), .S(S0));
endmodule

module Comparador (
  input  A3,
  input  A2,
  input  A1,
  input  A0,
  input  B3,
  input  B2,
  input  B1,
  input  B0,
  input  Enabler,
  output out_10
);

  wire and_1_out, and_2_out, and_3_out, and_4_out, not_1_out, not_2_out, not_3_out, not_4_out, xor_1_out,
       xor_2_out, xor_3_out, xor_4_out;

  xor xor_1 (xor_1_out, A3, B3);
  xor xor_2 (xor_2_out, A2, B2);
  xor xor_3 (xor_3_out, A1, B1);
  xor xor_4 (xor_4_out, A0, B0);
  not not_1 (not_1_out, xor_1_out);
  not not_2 (not_2_out, xor_2_out);
  not not_3 (not_3_out, xor_3_out);
  not not_4 (not_4_out, xor_4_out);
  and and_1 (and_1_out, not_1_out, Enabler);
  and and_2 (and_2_out, not_2_out, Enabler);
  and and_3 (and_3_out, not_3_out, Enabler);
  and and_4 (and_4_out, not_4_out, Enabler);
  and and_5 (out_10, and_1_out, and_2_out, and_3_out, and_4_out);
endmodule

module TrabalhoFinal1 (
  input  [3:0] A,
  input  [3:0] B,
  input  Enable,
  input  [2:0] in_4,
  output [4:0] out_5
);

  wire andy_1_s0, andy_1_s1, andy_1_s2, andy_1_s3, comparador_1_out_10, demux3_1_s0, demux3_1_s1,
       demux3_1_s2, demux3_1_s3, demux3_1_s4, demux3_1_s5, demux3_1_s6, demux3_1_s7, deslocador_1_s0,
       deslocador_1_s1, deslocador_1_s2, deslocador_1_s3, detectordezero_1_s, or2_1_s0, or2_1_s1, or2_1_s2,
       or2_1_s3, somador_4_bits_1_s0, somador_4_bits_1_s1, somador_4_bits_1_s2, somador_4_bits_1_s3,
       sub_com_vhl_e_sem_1_s0, sub_com_vhl_e_sem_1_s1, sub_com_vhl_e_sem_1_s2, sub_com_vhl_e_sem_1_s3,
       subcomplemento_1_s0, subcomplemento_1_s1, subcomplemento_1_s2, subcomplemento_1_s3;

  Demux3 demux3_1 (
    .A(Enable), .Sel3(in_4[2]), .Sel2(in_4[1]), .Sel1(in_4[0]), .S0(demux3_1_s0), .S1(demux3_1_s1),
    .S2(demux3_1_s2), .S3(demux3_1_s3), .S4(demux3_1_s4), .S5(demux3_1_s5), .S6(demux3_1_s6), .S7(demux3_1_s7));
  somador_4_bits somador_4_bits_1 (
    .A3(A[3]), .A2(A[2]), .A1(A[1]), .A0(A[0]), .B3(B[3]), .B2(B[2]), .B1(B[1]), .B0(B[0]),
    .ENABLER(demux3_1_s0), .S4(out_5[4]), .S3(somador_4_bits_1_s3), .S2(somador_4_bits_1_s2),
    .S1(somador_4_bits_1_s1), .S0(somador_4_bits_1_s0));
  sub_com_vhl_e_sem sub_com_vhl_e_sem_1 (
    .A3(A[3]), .A2(A[2]), .A1(A[1]), .A0(A[0]), .B3(B[3]), .B2(B[2]), .B1(B[1]), .B0(B[0]),
    .Enabler(demux3_1_s1), .S3(sub_com_vhl_e_sem_1_s3), .S2(sub_com_vhl_e_sem_1_s2),
    .S1(sub_com_vhl_e_sem_1_s1), .S0(sub_com_vhl_e_sem_1_s0));
  SubComplemento subcomplemento_1 (
    .A3(A[3]), .A2(A[2]), .A1(A[1]), .A0(A[0]), .B3(B[3]), .B2(B[2]), .B1(B[1]), .B0(B[0]),
    .Enabler(demux3_1_s2), .S3(subcomplemento_1_s3), .S2(subcomplemento_1_s2), .S1(subcomplemento_1_s1),
    .S0(subcomplemento_1_s0));
  andy andy_1 (
    .A3(A[3]), .A2(A[2]), .A1(A[1]), .A0(A[0]), .B3(B[3]), .B2(B[2]), .B1(B[1]), .B0(B[0]),
    .ENABLER(demux3_1_s3), .S3(andy_1_s3), .S2(andy_1_s2), .S1(andy_1_s1), .S0(andy_1_s0));
  OR2 or2_1 (
    .A3(A[3]), .A2(A[2]), .A1(A[1]), .A0(A[0]), .B3(B[3]), .B2(B[2]), .B1(B[1]), .B0(B[0]),
    .in_9(demux3_1_s4), .S3(or2_1_s3), .S2(or2_1_s2), .S1(or2_1_s1), .S0(or2_1_s0));
  deslocador deslocador_1 (
    .A3(A[3]), .A2(A[2]), .A1(A[1]), .A0(A[0]), .B1(B[1]), .B0(B[0]), .Enabler(demux3_1_s5),
    .S3(deslocador_1_s3), .S2(deslocador_1_s2), .S1(deslocador_1_s1), .S0(deslocador_1_s0));
  Comparador comparador_1 (
    .A3(A[3]), .A2(A[2]), .A1(A[1]), .A0(A[0]), .B3(B[3]), .B2(B[2]), .B1(B[1]), .B0(B[0]),
    .Enabler(demux3_1_s6), .out_10(comparador_1_out_10));
  DetectorDeZero detectordezero_1 (
    .A3(A[3]), .A2(A[2]), .A1(A[1]), .A0(A[0]), .enabler(demux3_1_s7), .S(detectordezero_1_s));
  or S3 (out_5[3], somador_4_bits_1_s3, sub_com_vhl_e_sem_1_s3, subcomplemento_1_s3, andy_1_s3, or2_1_s3, deslocador_1_s3);
  or S2 (out_5[2], somador_4_bits_1_s2, sub_com_vhl_e_sem_1_s2, subcomplemento_1_s2, andy_1_s2, or2_1_s2, deslocador_1_s2);
  or S1 (out_5[1], somador_4_bits_1_s1, sub_com_vhl_e_sem_1_s1, subcomplemento_1_s1, andy_1_s1, or2_1_s1, deslocador_1_s1);
  or S0 (out_5[0], somador_4_bits_1_s0, sub_com_vhl_e_sem_1_s0, subcomplemento_1_s0, andy_1_s0, or2_1_s0, deslocador_1_s0, comparador_1_out_10, detectordezero_1_s);
endmodule

module trabalhoFinal1VHDL (
  input  [3:0] A,
  input  [3:0] B,
  input  Enabler,
  input  [2:0] Sel,
  output [4:0] out_5
);

  wire comparadorvhdl_1_s, demuxvhdl_1_s0, demuxvhdl_1_s1, demuxvhdl_1_s2, demuxvhdl_1_s3, demuxvhdl_1_s4,
       demuxvhdl_1_s5, demuxvhdl_1_s6, demuxvhdl_1_s7, detectordezerovhdl_1_s;
  wire [3:0] andvhdl_1_s, deslocadorvhdl_1_s, orvhdl_1_s, subcomplemento_1_s, subtrator_4_bits_vhdl_1_s;
  wire [4:0] somador_vhdl_1_s;

  DemuxVHDL demuxvhdl_1 (
    .A(Enabler), .Sel(Sel), .S0(demuxvhdl_1_s0), .S1(demuxvhdl_1_s1), .S2(demuxvhdl_1_s2),
    .S3(demuxvhdl_1_s3), .S4(demuxvhdl_1_s4), .S5(demuxvhdl_1_s5), .S6(demuxvhdl_1_s6), .S7(demuxvhdl_1_s7));
  somador_vhdl somador_vhdl_1 (.A(A), .B(B), .ENABLER(demuxvhdl_1_s0), .S(somador_vhdl_1_s));
  subtrator_4_bits_vhdl subtrator_4_bits_vhdl_1 (.A(A), .B(B), .ENABLER(demuxvhdl_1_s1), .S(subtrator_4_bits_vhdl_1_s));
  subComplemento subcomplemento_1 (.A(A), .B(B), .ENABLER(demuxvhdl_1_s2), .S(subcomplemento_1_s));
  andVHDL andvhdl_1 (.A(A), .B(B), .ENABLER(demuxvhdl_1_s3), .S(andvhdl_1_s));
  ORVHDL orvhdl_1 (.A(A), .B(B), .ENABLER(demuxvhdl_1_s4), .S(orvhdl_1_s));
  DeslocadorVHDL deslocadorvhdl_1 (.A(A), .B(B), .C(demuxvhdl_1_s5), .S(deslocadorvhdl_1_s));
  ComparadorVHDL comparadorvhdl_1 (.A(A), .B(B), .ENABLER(demuxvhdl_1_s6), .S(comparadorvhdl_1_s));
  DetectorDeZeroVHDL detectordezerovhdl_1 (.A(A), .ENABLER(demuxvhdl_1_s7), .S(detectordezerovhdl_1_s));
  MuxVHDL muxvhdl_1 (
    .soma(somador_vhdl_1_s), .sub(subtrator_4_bits_vhdl_1_s), .subComp(subcomplemento_1_s),
    .andV(andvhdl_1_s), .orV(orvhdl_1_s), .deslocador(deslocadorvhdl_1_s), .comparador(comparadorvhdl_1_s),
    .detectorZero(detectordezerovhdl_1_s), .sel(Sel), .data_out(out_5));
endmodule

// VHDL entity somador_vhdl, as the project stores it:
LIBRARY ieee;
USE ieee.std_logic_1164.all;

ENTITY somador_vhdl IS
  PORT (
  ------------------------------------------------------------------------------
  --Insert input ports below
    A      : IN  std_logic_vector(3 DOWNTO 0);                   -- input bit example
    B       : IN  std_logic_vector(3 DOWNTO 0); -- input vector example
    ENABLER: IN std_logic;
  ------------------------------------------------------------------------------
  --Insert output ports below
                  -- output bit example
    S        : OUT std_logic_vector(4 DOWNTO 0)
    
    );
END somador_vhdl;


--------------------------------------------------------------------------------
--Complete your VHDL description below
--------------------------------------------------------------------------------

ARCHITECTURE TypeArchitecture OF somador_vhdl IS
signal carry : std_logic_vector(3 DOWNTO 0);
BEGIN
	process(A, B, ENABLER, carry)
	begin
		if (ENABLER = '1') then
			S(0) <= A(0) xor B(0);
			carry(1) <= A(0) and B(0);
			
			S(1) <= ((A(1) xor carry(1)) xor B(1));
			carry(2) <= (A(1) and carry(1)) or (B(1) and (A(1) xor carry(1)));
			
			S(2) <= ((A(2) xor carry(2)) xor B(2));
			carry(3) <= (A(2) and carry(2)) or (B(2) and (A(2) xor carry(2)));
			
			S(3) <= ((A(3) xor carry(3)) xor B(3));
			S(4) <= (A(3) and carry(3)) or (B(3) and (A(3) xor carry(3)));
		else
		S <= "00000";
		end if;
	end process;

END TypeArchitecture;

// VHDL entity subtrator_4_bits_vhdl, as the project stores it:
LIBRARY ieee;
USE ieee.std_logic_1164.all;

ENTITY subtrator_4_bits_vhdl IS
  PORT (
    A      : IN  std_logic_vector(3 DOWNTO 0); -- vetor de entrada A
    B      : IN  std_logic_vector(3 DOWNTO 0); -- vetor de entrada B
    ENABLER: IN  std_logic;
    S      : OUT std_logic_vector(3 DOWNTO 0)  -- vetor de saída S
  );
END subtrator_4_bits_vhdl;

ARCHITECTURE TypeArchitecture OF subtrator_4_bits_vhdl IS
  SIGNAL borrow : std_logic_vector(4 DOWNTO 0); -- vetores de borrow com bit extra para o último
BEGIN
  PROCESS (A, B, ENABLER, borrow)
  BEGIN
    -- Inicializa o borrow inicial como '0'
    
    
    IF (ENABLER = '1') THEN
    	 borrow(0) <= '0';
      FOR i IN 0 TO 3 LOOP
        S(i) <= A(i) XOR B(i) XOR borrow(i);
        borrow(i+1) <= ((NOT A(i)) AND borrow(i)) OR (((NOT A(i)) XNOR (NOT borrow(i))) AND B(i));
      END LOOP;
    ELSE
      S <= "0000";
    END IF;
  END PROCESS;
END TypeArchitecture;

// VHDL entity subComplemento, as the project stores it:
LIBRARY ieee;
USE ieee.std_logic_1164.all;
USE ieee.numeric_std.all;  -- For operations with unsigned

ENTITY subComplemento IS
  PORT (
    A      : IN  std_logic_vector(3 DOWNTO 0);  -- Input vector A
    B      : IN  std_logic_vector(3 DOWNTO 0);  -- Input vector B
    ENABLER: IN  std_logic;
    S      : OUT std_logic_vector(3 DOWNTO 0)   -- Output (A - B)
  );
END subComplemento;

ARCHITECTURE TypeArchitecture OF subComplemento IS
  signal result : unsigned(4 DOWNTO 0);  -- Result of the addition with an extra bit for carry
  SIGNAL B_complemento : unsigned(4 DOWNTO 0);
  SIGNAL B2 : unsigned(3 DOWNTO 0);
BEGIN
  process(A, B, ENABLER,B_complemento ,B2,result)

    -- Complement of B with extended bit width
  begin
    if (ENABLER = '1') then
      -- Extend and invert B to create the two's complement representation
      B_complemento <= not unsigned('0' & B) + 1;
	 B2 <= B_complemento(3 DOWNTO 0);
      -- Perform A - B using A + B_complemento
      result <= unsigned('0' & A) + unsigned('0' & B2);

      -- Assign the result to S, including the overflow bit
      S <= std_logic_vector(result(3 DOWNTO 0));
    else
      S <= "0000";
    end if;
  end process;
END TypeArchitecture;

// VHDL entity andVHDL, as the project stores it:
--------------------------------------------------------------------------------
-- Project :
-- File    :
-- Autor   :
-- Date    :
--
--------------------------------------------------------------------------------
-- Description :
--
--------------------------------------------------------------------------------

LIBRARY ieee;
USE ieee.std_logic_1164.all;

ENTITY andVHDL IS
  PORT (
  ------------------------------------------------------------------------------
  --Insert input ports below
    A        : IN  std_logic_vector(3 DOWNTO 0); -- input vector example
    B        : IN  std_logic_vector(3 DOWNTO 0);
    ENABLER : IN std_logic;
  ------------------------------------------------------------------------------
  --Insert output ports below
    S        : OUT std_logic_vector(3 DOWNTO 0)  -- output vector example
    );
END andVHDL;

--------------------------------------------------------------------------------
--Complete your VHDL description below
--------------------------------------------------------------------------------

ARCHITECTURE TypeArchitecture OF andVHDL IS

BEGIN
 	S<= A and B when ENABLER = '1' else "0000";

END TypeArchitecture;

// VHDL entity ORVHDL, as the project stores it:
--------------------------------------------------------------------------------
-- Project :
-- File    :
-- Autor   :
-- Date    :
--
--------------------------------------------------------------------------------
-- Description :
--
--------------------------------------------------------------------------------

LIBRARY ieee;
USE ieee.std_logic_1164.all;

ENTITY ORVHDL IS
  PORT (
  ------------------------------------------------------------------------------
  --Insert input ports below
    A        : IN  std_logic_vector(3 DOWNTO 0); -- input vector example
    B        : IN  std_logic_vector(3 DOWNTO 0);
    ENABLER : IN std_logic;
  ------------------------------------------------------------------------------
  --Insert output ports below
    S        : OUT std_logic_vector(3 DOWNTO 0)  -- output vector example
    );
END ORVHDL;

--------------------------------------------------------------------------------
--Complete your VHDL description below
--------------------------------------------------------------------------------

ARCHITECTURE TypeArchitecture OF ORVHDL IS

BEGIN
 	S<= A or B when ENABLER = '1' else "0000";

END TypeArchitecture;

// VHDL entity ComparadorVHDL, as the project stores it:
--------------------------------------------------------------------------------
-- Project :
-- File    :
-- Autor   :
-- Date    :
--
--------------------------------------------------------------------------------
-- Description :
--
--------------------------------------------------------------------------------

LIBRARY ieee;
USE ieee.std_logic_1164.all;

ENTITY ComparadorVHDL IS
  PORT (
  ------------------------------------------------------------------------------
  --Insert input ports below
    A        : IN  std_logic_vector(3 DOWNTO 0); -- input vector example
    B        : IN  std_logic_vector(3 DOWNTO 0);
    ENABLER : IN std_logic;
  ------------------------------------------------------------------------------
  --Insert output ports below
    S        : OUT std_logic  -- output vector example
    );
END ComparadorVHDL;

--------------------------------------------------------------------------------
--Complete your VHDL description below
--------------------------------------------------------------------------------

ARCHITECTURE TypeArchitecture OF ComparadorVHDL IS
BEGIN
  process(A, B)
  begin
    if A = B  AND ENABLER = '1' then
      S <= '1';  -- Example output when A equals B
    else
      S <= '0';  -- Example output when A does not equal B
    end if;
  end process;
END TypeArchitecture;

// VHDL entity DetectorDeZeroVHDL, as the project stores it:
--------------------------------------------------------------------------------
-- Project :
-- File    :
-- Autor   :
-- Date    :
--
--------------------------------------------------------------------------------
-- Description :
--
--------------------------------------------------------------------------------

LIBRARY ieee;
USE ieee.std_logic_1164.all;

ENTITY DetectorDeZeroVHDL IS
  PORT (
  ------------------------------------------------------------------------------
  --Insert input ports below
    A        : IN  std_logic_vector(3 DOWNTO 0); -- input vector example
    ENABLER : IN std_logic;
  ------------------------------------------------------------------------------
  --Insert output ports below
    S        : OUT std_logic  -- output vector example
    );
END DetectorDeZeroVHDL;

--------------------------------------------------------------------------------
--Complete your VHDL description below
--------------------------------------------------------------------------------

ARCHITECTURE TypeArchitecture OF DetectorDeZeroVHDL IS
BEGIN
  process(A)
  begin
    if A = "0000" AND ENABLER = '1' then
      S <= '1';  -- Example output when A equals B
    else
      S <= '0';  -- Example output when A does not equal B
    end if;
  end process;
END TypeArchitecture;

// VHDL entity DeslocadorVHDL, as the project stores it:
library IEEE;
use IEEE.STD_LOGIC_1164.ALL;
use IEEE.STD_LOGIC_ARITH.ALL;
use IEEE.STD_LOGIC_UNSIGNED.ALL;

entity DeslocadorVHDL is
    Port (
        A : in STD_LOGIC_VECTOR(3 downto 0);
        B : in STD_LOGIC_VECTOR(3 downto 0);
        C : in STD_LOGIC;
        S : out STD_LOGIC_VECTOR(3 downto 0)
    );
end DeslocadorVHDL;

architecture Behavioral of DeslocadorVHDL is
signal B2 : std_logic_vector(1 DOWNTO 0);
begin

    process(A, B, C, B2)
    
    begin
    B2 <= B(1) & B(0);
        if (C = '1') then
            case B2 is
                when "01" =>  -- Deslocamento para a direita
                    S <= '0' & a(3 downto 1);
                when "10" =>  -- Deslocamento para a esquerda
                    S <= a(2 downto 0) & '0';
                when others =>  -- Nenhuma operação
                    S <= A;
            end case;
        else
            S <= (others => '0');  -- Saída 0000 quando C é 0
        end if;
    end process;
end Behavioral;

// VHDL entity DemuxVHDL, as the project stores it:
library IEEE;
use IEEE.STD_LOGIC_1164.ALL;

entity DemuxVHDL is
    Port (
        A : in STD_LOGIC; -- Entrada
        Sel: in STD_LOGIC_VECTOR(2 DOWNTO 0);
        S0 : out STD_LOGIC; -- Saída 0
        S1 : out STD_LOGIC; -- Saída 1
        S2 : out STD_LOGIC; -- Saída 2
        S3 : out STD_LOGIC; -- Saída 3
        S4 : out STD_LOGIC; -- Saída 4
        S5 : out STD_LOGIC; -- Saída 5
        S6 : out STD_LOGIC; -- Saída 6
        S7 : out STD_LOGIC  -- Saída 7
    );
end DemuxVHDL;

architecture Behavioral of DemuxVHDL is
begin
    process(A, Sel)
    begin
    if (A = '1') then
        S0 <= (NOT Sel(2)) AND (NOT Sel(1)) AND (NOT Sel(0));
        S1 <= (NOT Sel(2)) AND (NOT Sel(1)) AND Sel(0);
        S2 <= (NOT Sel(2)) AND Sel(1) AND (NOT Sel(0));
        S3 <= (NOT Sel(2)) AND Sel(1) AND Sel(0);
        S4 <= Sel(2) AND (NOT Sel(1)) AND (NOT Sel(0));
        S5 <= Sel(2) AND (NOT Sel(1)) AND Sel(0);
        S6 <= Sel(2) AND Sel(1) AND (NOT Sel(0));
        S7 <= Sel(2) AND Sel(1) AND Sel(0);
    else
    	   S0 <= '0';
        S1 <= '0';
        S2 <= '0';
        S3 <= '0';
        S4 <= '0';
        S5 <= '0';
        S6 <= '0';
        S7 <= '0';
    end if;
    
    end process;
end Behavioral;

// VHDL entity MuxVHDL, as the project stores it:
LIBRARY ieee;
USE ieee.std_logic_1164.all;

ENTITY MuxVHDL IS
  PORT (
    soma : IN  std_logic_vector(4 DOWNTO 0);
    sub : IN  std_logic_vector(3 DOWNTO 0);
    subComp : IN  std_logic_vector(3 DOWNTO 0);
    andV : IN  std_logic_vector(3 DOWNTO 0);
    orV : IN  std_logic_vector(3 DOWNTO 0);
    deslocador : IN  std_logic_vector(3 DOWNTO 0);
    comparador : IN  std_logic;
    detectorZero : IN  std_logic;
    sel     : IN  std_logic_vector(2 DOWNTO 0); -- 3 bits de seleção
    data_out : OUT std_logic_vector(4 DOWNTO 0)                    -- Saída
  );
END MuxVHDL;

ARCHITECTURE Behavioral OF MuxVHDL IS
BEGIN
  process(soma,sub,subComp,andV,orV,deslocador,comparador,detectorZero,sel)
  begin
    case sel is
      when "000" => data_out <= soma;
      when "001" => data_out <= '0' & sub ;
      when "010" => data_out <= '0' & subComp;
      when "011" => data_out <= '0' & andV;
      when "100" => data_out <= '0' & orV;
      when "101" => data_out <= '0' & deslocador;
      when "110" => data_out <= "0000" & comparador;
      when "111" => data_out <= "0000" & detectorZero;
      when others => data_out <= "00000"; -- Caso indeterminado
    end case;
  end process;
END Behavioral;
