// Logisim project deslocaar.circ as structural Verilog
module seletor (
  input  nada,
  input  esquerda,
  input  Direita,
  input  [1:0] B,
  output S
);

  wire and_1_out, and_2_out, and_3_out, not_1_out, not_2_out, not_3_out, not_4_out;

  not not_1 (not_1_out, B[0]);
  not not_2 (not_2_out, B[1]);
  not not_3 (not_3_out, B[0]);
  not not_4 (not_4_out, B[1]);
  and and_1 (and_1_out, not_1_out, nada, not_2_out);
  and and_2 (and_2_out, not_3_out, esquerda, B[1]);
  and and_3 (and_3_out, B[0], Direita, not_4_out);
  or or_1 (S, and_1_out, and_2_out, and_3_out);
endmodule

module deslocamento (
  input  [3:0] in_1,
  input  [1:0] in_2,
  output [4:0] out_3
);

  deslocador deslocador_1 (.A(in_1), .B(in_2), .S(out_3));
endmodule

module seletor_cicuito (
  input  soma,
  input  B,
  input  Deslocar,
  output out_4
);

  wire and_1_out, and_2_out, not_1_out;

  not not_1 (not_1_out, B);
  and and_1 (and_1_out, soma, not_1_out);
  and and_2 (and_2_out, Deslocar, B);
  or or_1 (out_4, and_1_out, and_2_out);
endmodule

module deslocador (
  input  [3:0] A,
  input  [1:0] B,
  output [4:0] S
);

  seletor seletor_1 (.nada(1'b0), .esquerda(A[3]), .Direita(1'b0), .B(B), .S(S[4]));
  seletor seletor_2 (.nada(A[3]), .esquerda(A[2]), .Direita(1'b0), .B(B), .S(S[3]));
  seletor seletor_3 (.nada(A[2]), .esquerda(A[1]), .Direita(A[3]), .B(B), .S(S[2]));
  seletor seletor_4 (.nada(A[1]), .esquerda(A[0]), .Direita(A[2]), .B(B), .S(S[1]));
  seletor seletor_5 (.nada(A[0]), .esquerda(1'b0), .Direita(A[1]), .B(B), .S(S[0]));
endmodule
