// Logisim project flopFlip.circ as structural Verilog
module JKME (
  input  SET,
  input  J,
  input  COCK,
  input  K,
  input  RESET,
  output Q,
  output NQ
);

  wire nand_1_out, nand_2_out, nand_3_out, nand_4_out, nand_5_out, nand_6_out, not_1_out;

  nand nand_1 (nand_1_out, COCK, J, NQ);
  nand nand_2 (nand_2_out, Q, K, COCK);
  not not_1 (not_1_out, COCK);
  nand nand_3 (nand_3_out, SET, nand_1_out, nand_4_out);
  nand nand_4 (nand_4_out, nand_3_out, nand_2_out, RESET);
  nand nand_5 (nand_5_out, nand_3_out, not_1_out);
  nand nand_6 (nand_6_out, not_1_out, nand_4_out);
  nand nand_7 (Q, SET, nand_5_out, NQ);
  nand nand_8 (NQ, Q, nand_6_out, RESET);
endmodule

module FFT (
  input  SET,
  input  J,
  input  clk,
  input  CLEAR,
  output Q,
  output NQ
);

  JKME jkme_1 (.SET(SET), .J(J), .COCK(clk), .K(J), .RESET(CLEAR), .Q(Q), .NQ(NQ));
endmodule

module FFMEPSD (
  input  SET,
  input  J,
  input  CLK,
  input  CLEAR,
  output Q,
  output NQ
);

  wire not_1_out;

  not not_1 (not_1_out, J);
  JKME jkme_1 (.SET(SET), .J(J), .COCK(CLK), .K(not_1_out), .RESET(CLEAR), .Q(Q), .NQ(NQ));
endmodule

module conversor (
  input  AA,
  input  BB,
  input  CC,
  input  DD,
  output a,
  output b,
  output c,
  output d,
  output e,
  output f,
  output g
);

  wire and_1_out, and_2_out, and_3_out, and_4_out, and_5_out, and_6_out, and_7_out, and_8_out, and_9_out,
       and_10_out, and_11_out, and_12_out, and_13_out, and_14_out, and_15_out, and_16_out, and_17_out,
       and_18_out, and_19_out, and_20_out, and_21_out, and_22_out, and_23_out, and_24_out, and_25_out,
       and_26_out, and_27_out, and_28_out, and_29_out, and_30_out, and_31_out, and_32_out, and_33_out,
       and_34_out, and_35_out, not_1_out, not_2_out, not_3_out, not_4_out;

  not not_1 (not_1_out, AA);
  not not_2 (not_2_out, BB);
  not not_3 (not_3_out, CC);
  not not_4 (not_4_out, DD);
  and and_1 (and_1_out, not_2_out, not_4_out);
  and and_2 (and_2_out, not_1_out, CC);
  and and_3 (and_3_out, not_1_out, BB, DD);
  and and_4 (and_4_out, AA, not_2_out, not_3_out);
  and and_5 (and_5_out, AA, not_4_out);
  and and_6 (and_6_out, BB, CC);
  and and_7 (and_7_out, not_1_out, not_3_out, not_4_out);
  and and_8 (and_8_out, not_1_out, CC, DD);
  and and_9 (and_9_out, not_2_out, not_4_out);
  and and_10 (and_10_out, AA, not_3_out, DD);
  and and_11 (and_11_out, not_1_out, not_2_out);
  and and_12 (and_12_out, not_1_out, BB);
  and and_13 (and_13_out, AA, not_2_out);
  and and_14 (and_14_out, not_3_out, DD);
  and and_15 (and_15_out, not_2_out, not_3_out);
  and and_16 (and_16_out, not_2_out, DD);
  and and_17 (and_17_out, BB, not_3_out, DD);
  and and_18 (and_18_out, not_1_out, not_2_out, not_4_out);
  and and_19 (and_19_out, not_2_out, CC, DD);
  and and_20 (and_20_out, AA, not_3_out);
  and and_21 (and_21_out, BB, CC, not_4_out);
  and and_22 (and_22_out, not_2_out, not_4_out);
  and and_23 (and_23_out, CC, not_4_out);
  and and_24 (and_24_out, AA, CC);
  and and_25 (and_25_out, AA, BB);
  and and_26 (and_26_out, not_3_out, not_4_out);
  and and_27 (and_27_out, not_1_out, BB, not_3_out);
  and and_28 (and_28_out, BB, not_4_out);
  and and_29 (and_29_out, AA, not_2_out);
  and and_30 (and_30_out, AA, CC);
  and and_31 (and_31_out, not_2_out, CC);
  and and_32 (and_32_out, AA, not_2_out);
  and and_33 (and_33_out, not_1_out, BB, not_3_out);
  and and_34 (and_34_out, CC, not_4_out);
  and and_35 (and_35_out, AA, DD);
  or or_1 (a, and_1_out, and_2_out, and_3_out, and_4_out, and_5_out, and_6_out);
  or or_2 (b, and_7_out, and_8_out, and_9_out, and_10_out, and_11_out);
  or or_3 (c, and_12_out, and_13_out, and_14_out, and_15_out, and_16_out);
  or or_4 (d, and_17_out, and_18_out, and_19_out, and_20_out, and_21_out);
  or or_5 (e, and_22_out, and_23_out, and_24_out, and_25_out);
  or or_6 (f, and_26_out, and_27_out, and_28_out, and_29_out, and_30_out);
  or or_7 (g, and_31_out, and_32_out, and_33_out, and_34_out, and_35_out);
endmodule

module Registrador (
  input  SET,
  input  in_2,
  input  in_3,
  input  in_4,
  input  in_5,
  input  J,
  input  clk,
  input  CLEAR,
  output out_9,
  output out_10,
  output out_11,
  output out_12
);

  wire and_1_out, conversor_1_a, conversor_1_b, conversor_1_c, conversor_1_d, conversor_1_e, conversor_1_f,
       conversor_1_g, fft_1_nq, fft_1_q, nand_1_out, nand_2_out, nand_3_out, nand_4_out, not_1_out,
       not_2_out, not_3_out, not_4_out, not_5_out, not_6_out, not_7_out, not_8_out, not_9_out, not_10_out,
       not_11_out, not_12_out, not_13_out, xor_1_out;

  not not_1 (not_1_out, SET);
  FFT fft_1 (.SET(1'b1), .J(1'b1), .clk(not_1_out), .CLEAR(1'b1), .Q(fft_1_q), .NQ(fft_1_nq));
  and and_1 (and_1_out, SET, fft_1_q);
  nand nand_1 (nand_1_out, and_1_out, in_2);
  not not_2 (not_2_out, nand_1_out);
  not not_3 (not_3_out, not_2_out);
  not not_4 (not_4_out, xor_1_out);
  xor xor_1 (xor_1_out, fft_1_nq, CLEAR);
  FFMEPSD ffmepsd_1 (.SET(not_3_out), .J(J), .CLK(clk), .CLEAR(not_4_out), .Q(out_9));  // open: NQ
  nand nand_2 (nand_2_out, and_1_out, in_3);
  not not_5 (not_5_out, nand_2_out);
  not not_6 (not_6_out, not_5_out);
  not not_7 (not_7_out, xor_1_out);
  FFMEPSD ffmepsd_2 (.SET(not_6_out), .J(out_9), .CLK(clk), .CLEAR(not_7_out), .Q(out_10));  // open: NQ
  nand nand_3 (nand_3_out, and_1_out, in_4);
  not not_8 (not_8_out, nand_3_out);
  not not_9 (not_9_out, not_8_out);
  not not_10 (not_10_out, xor_1_out);
  FFMEPSD ffmepsd_3 (.SET(not_9_out), .J(out_10), .CLK(clk), .CLEAR(not_10_out), .Q(out_12));  // open: NQ
  nand nand_4 (nand_4_out, and_1_out, in_5);
  not not_11 (not_11_out, nand_4_out);
  not not_12 (not_12_out, not_11_out);
  not not_13 (not_13_out, xor_1_out);
  FFMEPSD ffmepsd_4 (.SET(not_12_out), .J(out_12), .CLK(clk), .CLEAR(not_13_out), .Q(out_11));  // open: NQ
  conversor conversor_1 (
    .AA(out_9), .BB(out_10), .CC(out_12), .DD(out_11), .a(conversor_1_a), .b(conversor_1_b),
    .c(conversor_1_c), .d(conversor_1_d), .e(conversor_1_e), .f(conversor_1_f), .g(conversor_1_g));
  _7_Segment_Display u_7_segment_display_1 (
    .g(conversor_1_g), .f(conversor_1_f), .a(conversor_1_a), .b(conversor_1_b), .e(conversor_1_e),
    .d(conversor_1_d), .c(conversor_1_c));  // open: dp
endmodule

module mux (
  input  Entrada1,
  input  Entrada2,
  input  sel,
  output out_4
);

  wire and_1_out, and_2_out;

  and and_1 (and_1_out, Entrada1, ~sel);  // AND_Gate
  and and_2 (and_2_out, Entrada2, sel);
  or or_1 (out_4, and_1_out, and_2_out);
endmodule
