// Logisim project circuitoSomador.circ as structural Verilog
module main (
  input  A0,
  input  B0,
  input  in_3,
  input  A1,
  input  B2,
  output U,
  output D,
  output C
);

  wire somador_1_over;

  somador somador_1 (.A(A0), .B(B0), .Cin(in_3), .S1(U), .Over(somador_1_over));
  somador somador_2 (.A(A1), .B(B2), .Cin(somador_1_over), .S1(D), .Over(C));
endmodule

module somador (
  input  A,
  input  B,
  input  Cin,
  output S1,
  output Over
);

  wire and_1_out, and_2_out, and_3_out, xor_1_out;

  xor xor_1 (xor_1_out, A, B);
  xor xor_2 (S1, xor_1_out, Cin);
  and and_1 (and_1_out, A, B);
  and and_2 (and_2_out, A, Cin);
  and and_3 (and_3_out, B, Cin);
  or or_1 (Over, and_1_out, and_2_out, and_3_out);
endmodule

module subtrator (
  input  A,
  input  B,
  output S1,
  output out_4
);

  wire not_1_out;

  not not_1 (not_1_out, A);
  xor xor_1 (S1, A, B);
  and and_1 (out_4, not_1_out, B);
endmodule
