// Logisim project sumSub.circ as structural Verilog
module main (
  input  in_1,
  input  in_2,
  input  in_3,
  input  in_4,
  input  in_5,
  input  in_6,
  input  in_7,
  input  in_8,
  input  in_9,
  output out_10,
  output out_11,
  output out_12,
  output out_13,
  output out_14,
  output out_15,
  output [3:0] out_16
);

  sumSub4bits sumsub4bits_1 (
    .M(in_1), .A0(in_2), .A1(in_3), .A2(in_4), .A3(in_5), .B0(in_6), .B1(in_7), .B2(in_8), .B3(in_9),
    .S0(out_10), .S1(out_11), .S2(out_12), .S3(out_13), .OVER(out_14));
  sumSubVHDL sumsubvhdl_1 (
    .A({in_5, in_4, in_3, in_2}), .B({in_9, in_8, in_7, in_6}), .M(in_1), .ov(out_15), .S(out_16));
endmodule

module meioSumSub (
  input  M,
  input  A,
  input  B,
  output S,
  output C
);

  wire and_1_out, and_2_out, and_3_out, and_4_out, not_1_out, not_2_out, not_3_out;

  not not_1 (not_1_out, M);
  not not_2 (not_2_out, A);
  not not_3 (not_3_out, B);
  and and_1 (and_1_out, not_2_out, B);
  or or_1 (S, and_1_out, and_2_out);
  and and_2 (and_2_out, A, not_3_out);
  and and_3 (and_3_out, not_1_out, A, B);
  or or_2 (C, and_3_out, and_4_out);
  and and_4 (and_4_out, M, not_2_out, B);
endmodule

module sumSub4bits (
  input  M,
  input  A0,
  input  A1,
  input  A2,
  input  A3,
  input  B0,
  input  B1,
  input  B2,
  input  B3,
  output S0,
  output S1,
  output S2,
  output S3,
  output OVER
);

  wire sumsubcompleto_1_carry, sumsubcompleto_2_carry, sumsubcompleto_3_carry;

  sumSubCompleto sumsubcompleto_1 (.M(M), .A(A0), .B(B0), .Cin(1'b0), .S(S0), .Carry(sumsubcompleto_1_carry));
  sumSubCompleto sumsubcompleto_2 (
    .M(M), .A(A1), .B(B1), .Cin(sumsubcompleto_1_carry), .S(S1), .Carry(sumsubcompleto_2_carry));
  sumSubCompleto sumsubcompleto_3 (
    .M(M), .A(A2), .B(B2), .Cin(sumsubcompleto_2_carry), .S(S2), .Carry(sumsubcompleto_3_carry));
  sumSubCompleto sumsubcompleto_4 (.M(M), .A(A3), .B(B3), .Cin(sumsubcompleto_3_carry), .S(S3), .Carry(OVER));
endmodule

module sumSubCompleto (
  input  M,
  input  A,
  input  B,
  input  Cin,
  output S,
  output Carry
);

  wire meiosumsub_1_c, meiosumsub_1_s, meiosumsub_2_c;

  meioSumSub meiosumsub_1 (.M(M), .A(A), .B(Cin), .S(meiosumsub_1_s), .C(meiosumsub_1_c));
  meioSumSub meiosumsub_2 (.M(M), .A(meiosumsub_1_s), .B(B), .S(S), .C(meiosumsub_2_c));
  or or_1 (Carry, meiosumsub_1_c, meiosumsub_2_c);
endmodule

// VHDL entity sumSubVHDL, as the project stores it:
--------------------------------------------------------------------------------
-- Project :
-- File    :
-- Autor   :
-- Date    :
--
--------------------------------------------------------------------------------
-- Description :
--
--------------------------------------------------------------------------------

LIBRARY ieee;
USE ieee.std_logic_1164.all;

ENTITY sumSubVHDL IS
  PORT (
  ------------------------------------------------------------------------------
  --Insert input ports below
    A        : IN  std_logic_vector(3 DOWNTO 0);                    -- input bit example
    B        : IN  std_logic_vector(3 DOWNTO 0); -- input vector example
    M        : IN  std_logic;
    ov       : OUT  std_logic;
    S        : OUT std_logic_vector(3 DOWNTO 0)  -- output vector example
    );
END sumSubVHDL;

--------------------------------------------------------------------------------
--Complete your VHDL description below
--------------------------------------------------------------------------------

ARCHITECTURE TypeArchitecture OF sumSubVHDL IS
signal C : std_logic_vector(3 DOWNTO 0);
BEGIN
	S(0) <= A(0) XOR B(0);
	C(1) <= B(0) AND (M XOR A(0));
	
	S(1) <= B(1) XOR (A(1) XOR C(1));
	C(2) <= (B(1) AND ((M XOR A(1)) XOR C(1))) OR ((M XOR A(1)) AND C(1));
	
	S(2) <= B(2) XOR (A(2) XOR C(2));
	C(3) <= (B(2) AND ((M XOR A(2)) XOR C(2))) OR ((M XOR A(2)) AND C(2));

	S(3) <= B(3) XOR (A(3) XOR C(3));
	ov <= (B(3) AND ((M XOR A(3)) XOR C(3))) OR ((M XOR A(3)) AND C(3));
	
END TypeArchitecture;
